// Logisim project Exemplo_0501.circ as structural Verilog: 1 circuit, main circuit main
module main (
  input  in_1,
  input  in_2,
  input  in_3,
  input  in_4,
  input  in_5,
  input  in_6,
  input  in_7,
  input  in_8,
  input  in_9,
  input  in_10,
  input  in_11,
  input  in_12,
  input  in_13,
  input  in_14,
  input  in_15,
  input  in_16,
  output out_17,
  output out_18,
  output out_19,
  output out_20,
  output out_21,
  output out_22,
  output out_23,
  output out_24
);

  wire not_1_out, not_2_out, not_3_out, not_4_out, not_5_out, not_6_out, not_7_out, not_8_out, not_9_out,
       not_10_out, not_11_out, not_12_out, not_13_out, not_14_out, not_15_out, not_16_out, not_17_out,
       not_18_out, not_19_out, not_20_out, s1_2_out, s1_3_out, s1_4_out, s1_out, w1_2_out, w1_3_out,
       w1_4_out, w1_out, w2_2_out, w2_3_out, w2_4_out, w2_out, w3_2_out, w3_3_out, w3_4_out, w3_out;

  not not_1 (not_1_out, in_2);
  not not_2 (not_2_out, in_3);
  not not_3 (not_3_out, in_4);
  not not_4 (not_4_out, in_6);
  not not_5 (not_5_out, in_8);
  not not_6 (not_6_out, in_9);
  not not_7 (not_7_out, in_10);
  not not_8 (not_8_out, in_11);
  and and_1 (out_17, not_1_out, not_2_out);
  and and_2 (out_19, not_3_out, not_4_out);
  and and_3 (out_20, not_5_out, not_6_out);
  and and_4 (out_22, not_7_out, not_8_out);
  and w1 (w1_out, in_1, in_1);
  and w2 (w2_out, in_5, in_5);
  and w1_2 (w1_2_out, in_7, in_7);
  and w2_2 (w2_2_out, in_12, in_12);
  and w1_3 (w1_3_out, in_13, in_13);
  and w2_3 (w2_3_out, in_14, in_14);
  and w1_4 (w1_4_out, in_15, in_15);
  and w2_4 (w2_4_out, in_16, in_16);
  not not_9 (not_9_out, w1_out);
  and w3 (w3_out, not_9_out, not_10_out);
  not not_10 (not_10_out, w2_out);
  not not_11 (not_11_out, w1_2_out);
  and w3_2 (w3_2_out, not_11_out, not_12_out);
  not not_12 (not_12_out, w2_2_out);
  not not_13 (not_13_out, w1_3_out);
  and w3_3 (w3_3_out, not_13_out, not_14_out);
  not not_14 (not_14_out, w2_3_out);
  not not_15 (not_15_out, w1_4_out);
  and w3_4 (w3_4_out, not_15_out, not_16_out);
  not not_16 (not_16_out, w2_4_out);
  not not_17 (not_17_out, w3_out);
  not not_18 (not_18_out, w3_2_out);
  not not_19 (not_19_out, w3_3_out);
  not not_20 (not_20_out, w3_4_out);
  and s1 (s1_out, not_17_out, not_17_out);
  not not_21 (out_18, s1_out);
  and s1_2 (s1_2_out, not_18_out, not_18_out);
  not not_22 (out_21, s1_2_out);
  and s1_3 (s1_3_out, not_19_out, not_19_out);
  not not_23 (out_23, s1_3_out);
  not not_24 (out_24, s1_4_out);
  and s1_4 (s1_4_out, not_20_out, not_20_out);

  // Notes on the sheet:
  //   referencial
  //   (~a & ~b)
endmodule
