// Logisim project Exemplo_0504.circ as structural Verilog: 1 circuit, main circuit main
module main (
  input  in_1,
  input  in_2,
  input  in_3,
  input  in_4,
  input  in_5,
  input  in_6,
  input  in_7,
  input  in_8,
  input  in_9,
  input  in_10,
  input  in_11,
  input  in_12,
  input  in_13,
  input  in_14,
  input  in_15,
  input  in_16,
  output out_17,
  output out_18,
  output out_19,
  output out_20,
  output out_21,
  output out_22,
  output out_23,
  output out_24
);

  wire not_1_out, not_2_out, not_3_out, not_4_out, not_5_out, not_6_out, not_7_out, not_8_out, w_1_2_out,
       w_1_3_out, w_1_4_out, w_1_out, w_2_2_out, w_2_3_out, w_2_4_out, w_2_out;

  not not_1 (not_1_out, in_4);
  and and_1 (out_18, not_1_out, in_5);
  not not_2 (not_2_out, in_6);
  and and_2 (out_20, not_2_out, in_8);
  not not_3 (not_3_out, in_10);
  and and_3 (out_21, not_3_out, in_11);
  not not_4 (not_4_out, in_12);
  and and_4 (out_23, not_4_out, in_13);
  or w_1 (w_1_out, in_2, in_2);
  not not_5 (not_5_out, w_1_out);
  or w_1_2 (w_1_2_out, in_7, in_7);
  not not_6 (not_6_out, w_1_2_out);
  not not_7 (not_7_out, w_1_3_out);
  or w_1_3 (w_1_3_out, in_14, in_14);
  not not_8 (not_8_out, w_1_4_out);
  or w_1_4 (w_1_4_out, in_16, in_16);
  or w_2 (w_2_out, in_1, not_5_out);
  not not_9 (out_17, w_2_out);
  or w_2_2 (w_2_2_out, in_3, not_6_out);
  not not_10 (out_19, w_2_2_out);
  or w_2_3 (w_2_3_out, in_9, not_7_out);
  not not_11 (out_22, w_2_3_out);
  or w_2_4 (w_2_4_out, in_15, not_8_out);
  not not_12 (out_24, w_2_4_out);

  // Notes on the sheet:
  //   referencial
  //   (~A & B)
endmodule
