// Logisim project Exemplo_0505.circ as structural Verilog: 1 circuit, main circuit main
module main (
  input  in_1,
  input  in_2,
  input  in_3,
  input  in_4,
  input  in_5,
  input  in_6,
  input  in_7,
  input  in_8,
  input  in_9,
  input  in_10,
  input  in_11,
  input  in_12,
  input  in_13,
  input  in_14,
  input  in_15,
  input  in_16,
  output out_17,
  output out_18,
  output out_19,
  output out_20,
  output out_21,
  output out_22,
  output out_23,
  output out_24
);

  wire and_1_out, and_2_out, and_3_out, and_4_out, and_5_out, and_6_out, and_7_out, and_8_out, not_1_out,
       not_2_out, not_3_out, not_4_out, not_5_out, not_6_out, not_7_out, not_8_out, not_9_out, not_10_out,
       not_11_out, not_12_out, not_13_out, not_14_out, not_15_out, not_16_out, not_17_out, not_18_out,
       not_19_out, not_20_out, not_21_out, not_22_out, not_23_out, not_24_out, s1_2_out, s1_3_out, s1_4_out,
       s1_out, w_1_2_out, w_1_3_out, w_1_4_out, w_1_out, w_2_2_out, w_2_3_out, w_2_4_out, w_2_out, w_3_2_out,
       w_3_3_out, w_3_4_out, w_3_out, w_4_2_out, w_4_3_out, w_4_4_out, w_4_out;

  not not_1 (not_1_out, in_3);
  and and_1 (and_1_out, not_1_out, not_2_out);
  not not_2 (not_2_out, in_4);
  and and_2 (and_2_out, in_4, in_3);
  not not_3 (not_3_out, in_6);
  and and_3 (and_3_out, not_3_out, not_4_out);
  not not_4 (not_4_out, in_8);
  and and_4 (and_4_out, in_8, in_6);
  not not_5 (not_5_out, in_9);
  and and_5 (and_5_out, not_5_out, not_6_out);
  not not_6 (not_6_out, in_10);
  and and_6 (and_6_out, in_10, in_9);
  not not_7 (not_7_out, in_12);
  and and_7 (and_7_out, not_7_out, not_8_out);
  not not_8 (not_8_out, in_14);
  and and_8 (and_8_out, in_14, in_12);
  or or_1 (out_18, and_1_out, and_2_out);
  or or_2 (out_19, and_3_out, and_4_out);
  or or_3 (out_21, and_5_out, and_6_out);
  or or_4 (out_22, and_7_out, and_8_out);
  not not_9 (not_9_out, w_1_out);
  and w_1 (w_1_out, in_1, in_2);
  not not_10 (not_10_out, w_2_out);
  and w_2 (w_2_out, in_1, in_1);
  and w_3 (w_3_out, in_2, in_2);
  not not_11 (not_11_out, w_3_out);
  not not_12 (not_12_out, w_1_2_out);
  and w_1_2 (w_1_2_out, in_5, in_7);
  and w_2_2 (w_2_2_out, in_5, in_5);
  not not_13 (not_13_out, w_2_2_out);
  not not_14 (not_14_out, w_3_2_out);
  and w_3_2 (w_3_2_out, in_7, in_7);
  and w_1_3 (w_1_3_out, in_11, in_13);
  not not_15 (not_15_out, w_1_3_out);
  and w_2_3 (w_2_3_out, in_11, in_11);
  not not_16 (not_16_out, w_2_3_out);
  and w_3_3 (w_3_3_out, in_13, in_13);
  not not_17 (not_17_out, w_3_3_out);
  and w_1_4 (w_1_4_out, in_15, in_16);
  not not_18 (not_18_out, w_1_4_out);
  and w_2_4 (w_2_4_out, in_15, in_15);
  not not_19 (not_19_out, w_2_4_out);
  and w_3_4 (w_3_4_out, in_16, in_16);
  not not_20 (not_20_out, w_3_4_out);
  and w_4 (w_4_out, not_10_out, not_11_out);
  not not_21 (not_21_out, w_4_out);
  not not_22 (not_22_out, w_4_2_out);
  and w_4_2 (w_4_2_out, not_13_out, not_14_out);
  not not_23 (not_23_out, w_4_3_out);
  and w_4_3 (w_4_3_out, not_16_out, not_17_out);
  not not_24 (not_24_out, w_4_4_out);
  and w_4_4 (w_4_4_out, not_19_out, not_20_out);
  not not_25 (out_17, s1_out);
  and s1 (s1_out, not_9_out, not_21_out);
  not not_26 (out_20, s1_2_out);
  and s1_2 (s1_2_out, not_12_out, not_22_out);
  not not_27 (out_23, s1_3_out);
  and s1_3 (s1_3_out, not_15_out, not_23_out);
  not not_28 (out_24, s1_4_out);
  and s1_4 (s1_4_out, not_18_out, not_24_out);

  // Notes on the sheet:
  //   referencial
  //   (A xnor B)
endmodule
