// Logisim project Exemplo_0507.circ as structural Verilog: 1 circuit, main circuit main
module main (
  input  in_1,
  input  in_2,
  input  not_a__not_b,
  input  in_4,
  input  in_5,
  input  in_6,
  input  in_7,
  input  in_8,
  input  in_9,
  input  in_10,
  input  in_11,
  input  in_12,
  input  in_13,
  input  in_14,
  input  in_15,
  input  in_16,
  output out_17,
  output out_18,
  output out_19,
  output out_20,
  output out_21,
  output out_22,
  output out_23,
  output out_24
);

  wire and_1_out, and_2_out, and_3_out, and_4_out, and_5_out, and_6_out, and_7_out, and_8_out, not_1_out,
       not_2_out, not_3_out, not_4_out, not_5_out, not_6_out, not_7_out, not_8_out, not_9_out, not_10_out,
       not_11_out, not_12_out, not_13_out, not_14_out, not_15_out, not_16_out, not_21_out, not_22_out,
       not_23_out, not_24_out, not_25_out, not_26_out, not_27_out, not_28_out, not_29_out, not_30_out,
       not_31_out, not_32_out, not_33_out, not_34_out, not_35_out, not_36_out, or_1_out, or_2_out, or_3_out,
       or_4_out, s1_2_out, s1_3_out, s1_4_out, s1_out, w_1_2_out, w_1_3_out, w_1_4_out, w_1_out, w_2_2_out,
       w_2_3_out, w_2_4_out, w_2_out, w_3_2_out, w_3_3_out, w_3_4_out, w_3_out, w_4_2_out, w_4_3_out,
       w_4_4_out, w_4_out;

  not not_1 (not_1_out, not_a__not_b);
  not not_2 (not_2_out, in_4);
  not not_3 (not_3_out, not_2_out);
  not not_4 (not_4_out, not_1_out);
  not not_5 (not_5_out, in_7);
  not not_6 (not_6_out, in_8);
  not not_7 (not_7_out, not_6_out);
  not not_8 (not_8_out, not_5_out);
  not not_9 (not_9_out, in_9);
  not not_10 (not_10_out, not_11_out);
  not not_11 (not_11_out, in_11);
  not not_12 (not_12_out, not_9_out);
  not not_13 (not_13_out, in_13);
  not not_14 (not_14_out, not_15_out);
  not not_15 (not_15_out, in_14);
  not not_16 (not_16_out, not_13_out);
  and and_1 (and_1_out, not_1_out, not_3_out);
  and and_2 (and_2_out, not_4_out, not_2_out);
  and and_3 (and_3_out, not_5_out, not_7_out);
  and and_4 (and_4_out, not_8_out, not_6_out);
  and and_5 (and_5_out, not_9_out, not_10_out);
  and and_6 (and_6_out, not_12_out, not_11_out);
  and and_7 (and_7_out, not_13_out, not_14_out);
  and and_8 (and_8_out, not_16_out, not_15_out);
  or or_1 (or_1_out, and_1_out, and_2_out);
  or or_2 (or_2_out, and_3_out, and_4_out);
  or or_3 (or_3_out, and_5_out, and_6_out);
  or or_4 (or_4_out, and_7_out, and_8_out);
  not not_17 (out_18, or_1_out);
  not not_18 (out_20, or_2_out);
  not not_19 (out_21, or_3_out);
  not not_20 (out_23, or_4_out);
  and w_1 (w_1_out, in_1, in_2);
  not not_21 (not_21_out, w_1_out);
  not not_22 (not_22_out, w_2_out);
  and w_2 (w_2_out, in_1, in_1);
  not not_23 (not_23_out, w_3_out);
  and w_3 (w_3_out, in_2, in_2);
  and w_1_2 (w_1_2_out, in_5, in_6);
  not not_24 (not_24_out, w_1_2_out);
  and w_2_2 (w_2_2_out, in_5, in_5);
  not not_25 (not_25_out, w_2_2_out);
  not not_26 (not_26_out, w_3_2_out);
  and w_3_2 (w_3_2_out, in_6, in_6);
  and w_1_3 (w_1_3_out, in_10, in_12);
  not not_27 (not_27_out, w_1_3_out);
  and w_2_3 (w_2_3_out, in_10, in_10);
  not not_28 (not_28_out, w_2_3_out);
  and w_3_3 (w_3_3_out, in_12, in_12);
  not not_29 (not_29_out, w_3_3_out);
  and w_1_4 (w_1_4_out, in_15, in_16);
  not not_30 (not_30_out, w_1_4_out);
  not not_31 (not_31_out, w_2_4_out);
  and w_2_4 (w_2_4_out, in_15, in_15);
  and w_3_4 (w_3_4_out, in_16, in_16);
  not not_32 (not_32_out, w_3_4_out);
  and w_4 (w_4_out, not_22_out, not_23_out);
  not not_33 (not_33_out, w_4_out);
  and w_4_2 (w_4_2_out, not_25_out, not_26_out);
  not not_34 (not_34_out, w_4_2_out);
  and w_4_3 (w_4_3_out, not_28_out, not_29_out);
  not not_35 (not_35_out, w_4_3_out);
  and w_4_4 (w_4_4_out, not_31_out, not_32_out);
  not not_36 (not_36_out, w_4_4_out);
  and s1 (s1_out, not_21_out, not_33_out);
  not not_37 (out_17, s1_out);
  not not_38 (out_19, s1_2_out);
  and s1_2 (s1_2_out, not_24_out, not_34_out);
  and s1_3 (s1_3_out, not_27_out, not_35_out);
  not not_39 (out_22, s1_3_out);
  not not_40 (out_24, s1_4_out);
  and s1_4 (s1_4_out, not_30_out, not_36_out);

  // Notes on the sheet:
  //   referencial
  //   ~(~a ^ ~b)
  //   Essa equacao pode ser simplificada em um XNOR
  //   xor
  //   not
endmodule
