// Logisim project Exemplo_0508.circ as structural Verilog: 1 circuit, main circuit main
module main (
  input  in_1,
  input  in_2,
  input  na,
  input  in_4,
  input  in_5,
  input  in_6,
  input  in_7,
  input  in_8,
  input  in_9,
  input  in_10,
  input  in_11,
  input  in_12,
  input  in_13,
  input  in_14,
  input  in_15,
  input  in_16,
  output out_17,
  output out_18,
  output out_19,
  output out_20,
  output out_21,
  output out_22,
  output out_23,
  output out_24
);

  wire and_1_out, and_2_out, and_3_out, and_4_out, not_1_out, not_2_out, not_3_out, not_4_out, not_9_out,
       not_10_out, not_11_out, not_12_out, not_13_out, not_14_out, not_15_out, not_16_out, s1_2_out,
       s1_3_out, s1_4_out, s1_out, w_1_2_out, w_1_3_out, w_1_4_out, w_1_out, w_2_2_out, w_2_3_out, w_2_4_out,
       w_2_out;

  not not_1 (not_1_out, na);
  not not_2 (not_2_out, in_7);
  not not_3 (not_3_out, in_10);
  not not_4 (not_4_out, in_13);
  and and_1 (and_1_out, not_1_out, in_5);
  and and_2 (and_2_out, not_2_out, in_8);
  and and_3 (and_3_out, not_3_out, in_11);
  and and_4 (and_4_out, not_4_out, in_14);
  not not_5 (out_18, and_1_out);
  not not_6 (out_20, and_2_out);
  not not_7 (out_21, and_3_out);
  not not_8 (out_23, and_4_out);
  or w_1 (w_1_out, in_2, in_2);
  not not_9 (not_9_out, w_1_out);
  or w_1_2 (w_1_2_out, in_6, in_6);
  not not_10 (not_10_out, w_1_2_out);
  not not_11 (not_11_out, w_1_3_out);
  or w_1_3 (w_1_3_out, in_12, in_12);
  or w_1_4 (w_1_4_out, in_16, in_16);
  not not_12 (not_12_out, w_1_4_out);
  or w_2 (w_2_out, in_1, not_9_out);
  not not_13 (not_13_out, w_2_out);
  or w_2_2 (w_2_2_out, in_4, not_10_out);
  not not_14 (not_14_out, w_2_2_out);
  not not_15 (not_15_out, w_2_3_out);
  or w_2_3 (w_2_3_out, in_9, not_11_out);
  not not_16 (not_16_out, w_2_4_out);
  or w_2_4 (w_2_4_out, in_15, not_12_out);
  or s1 (s1_out, not_13_out, not_13_out);
  not not_17 (out_17, s1_out);
  not not_18 (out_19, s1_2_out);
  or s1_2 (s1_2_out, not_14_out, not_14_out);
  not not_19 (out_22, s1_3_out);
  or s1_3 (s1_3_out, not_15_out, not_15_out);
  not not_20 (out_24, s1_4_out);
  or s1_4 (s1_4_out, not_16_out, not_16_out);

  // Notes on the sheet:
  //   referencial
  //   ~(~a & b)
  //   Essa equacao pode ser simplificada em (a | ~b)
  //   ~a & b
  //   ~(~a&b)
endmodule
