// Logisim project exercicio7.circ as structural Verilog: 1 circuit, main circuit main
module main (
  input  X,
  input  Y,
  input  Z,
  output out_4
);

  wire not_1_out, not_2_out, not_3_out, or_1_out, or_2_out;

  not not_1 (not_1_out, Y);
  not not_2 (not_2_out, Z);
  not not_3 (not_3_out, X);
  or or_1 (or_1_out, not_1_out, not_2_out);
  or or_2 (or_2_out, not_3_out, Y, Z);
  and and_1 (out_4, or_1_out, or_2_out);
endmodule
