// Logisim project mux_demux.circ as structural Verilog: 1 circuit, main circuit main
module main (
  input  select_s,
  input  _0,
  input  _1,
  input  _2,
  input  _3,
  input  input_a_x,
  input  input_b_y,
  input  e0,
  input  e1,
  input  e0_2,
  input  e1_2,
  input  _0_2,
  input  _1_2,
  input  _2_2,
  input  _3_2,
  output output_s_z,
  output _0_3,
  output _1_3,
  output _2_3,
  output _3_3,
  output _0_4,
  output _1_4,
  output _2_4,
  output _3_4
);

  wire and1_out, and2_out, and_1_out, and_3_out, and_4_out, and_5_out, and_6_out, and_7_out, and_8_out,
       and_11_out, nd1_out, nd4_out, not_1_out, not_2_out, not_3_out, not_5_out, not_6_out, not_7_out,
       not_8_out, not_9_out, not_10_out, not_11_out, not_12_out, or_1_out, or_2_out;

  and nd1 (nd1_out, select_s, select_s);
  not not_1 (not_1_out, nd1_out);
  and and1 (and1_out, not_1_out, input_a_x);
  not not_2 (not_2_out, and1_out);
  and and2 (and2_out, select_s, input_b_y);
  not not_3 (not_3_out, and2_out);
  not not_4 (output_s_z, nd4_out);
  and nd4 (nd4_out, not_2_out, not_3_out);
  not not_5 (not_5_out, e1);
  not not_6 (not_6_out, e0);
  not not_7 (not_7_out, e0);
  not not_8 (not_8_out, e1);
  and and_1 (and_1_out, not_6_out, not_5_out, _0);
  and and_2 (_0_3, not_7_out, not_8_out, or_1_out);
  not not_9 (not_9_out, e1_2);
  not not_10 (not_10_out, e0_2);
  and and_3 (and_3_out, not_10_out, not_9_out, _0_2);
  and and_4 (and_4_out, not_10_out, e1_2, _1_2);
  and and_5 (and_5_out, e0_2, not_9_out, _2_2);
  and and_6 (and_6_out, e0_2, e1_2, _3_2);
  and and_7 (and_7_out, not_6_out, e1, _1);
  and and_8 (and_8_out, e0, not_5_out, _2);
  or or_1 (or_1_out, and_1_out, and_7_out, and_8_out, and_11_out);
  and and_9 (_2_3, e0, not_8_out, or_1_out);
  and and_10 (_1_3, not_7_out, e1, or_1_out);
  or or_2 (or_2_out, and_3_out, and_4_out, and_5_out, and_6_out);
  and and_11 (and_11_out, e0, e1, _3);
  and and_12 (_3_3, e0, e1, or_1_out);
  not not_11 (not_11_out, e1_2);
  not not_12 (not_12_out, e0_2);
  and and_13 (_0_4, not_12_out, not_11_out, or_2_out);
  and and_14 (_1_4, not_12_out, e1_2, or_2_out);
  and and_15 (_2_4, e0_2, not_11_out, or_2_out);
  and and_16 (_3_4, e0_2, e1_2, or_2_out);

  // Notes on the sheet:
  //   not_select
  //   select
  //   QUESTAO 1
  //   sa
  //   sb
  //   Estudo pessoal sobre multiplexador ligado a desmultiplexador
  //   Vertical
  //   Horizontal
endmodule
