// Logisim project exemplo0801.circ as structural Verilog: 1 circuit, main circuit main
module main (
  input  sinal,
  input  in_2,
  input  in_3,
  input  in_4,
  input  in_5,
  input  sinal_2,
  input  in_7,
  input  in_8,
  input  in_9,
  input  in_10,
  input  sinal_3,
  input  in_12,
  input  in_13,
  input  in_14,
  input  in_15,
  input  sinal_4,
  input  in_17,
  input  in_18,
  input  in_19,
  input  in_20,
  input  sinal_5,
  input  in_22,
  input  in_23,
  input  in_24,
  input  in_25,
  input  sinal_6,
  input  in_27,
  input  in_28,
  input  in_29,
  input  in_30,
  output sinal_7,
  output out_32,
  output out_33,
  output out_34,
  output out_35,
  output sinal_8,
  output out_37,
  output out_38,
  output out_39,
  output out_40,
  output sinal_9,
  output out_42,
  output out_43,
  output out_44,
  output out_45
);

  wire adder_1_cout, adder_2_cout, adder_3_cout, adder_4_cout, adder_5_cout, and_1_out, and_2_out, and_3_out,
       and_4_out, and_5_out, and_6_out, and_7_out, and_8_out, and_9_out, and_10_out, and_11_out, and_12_out,
       and_13_out, and_14_out, and_15_out, and_16_out, and_17_out, and_18_out, and_19_out, and_20_out,
       and_21_out, and_22_out, and_23_out, and_24_out, and_25_out, and_26_out, and_27_out, and_28_out,
       and_29_out, and_30_out, and_31_out, and_32_out, and_33_out, and_34_out, and_35_out, and_36_out,
       and_37_out, and_38_out, and_39_out, and_40_out, and_41_out, and_42_out, and_43_out, and_44_out,
       and_45_out, and_46_out, and_47_out, and_48_out, and_49_out, and_50_out, not_1_out, not_2_out,
       not_3_out, not_4_out, not_5_out, not_6_out, not_7_out, not_8_out, not_9_out, not_10_out, not_11_out,
       not_12_out, not_13_out, not_14_out, not_15_out, or_1_out, or_2_out, or_3_out, or_4_out, or_5_out,
       or_6_out, or_8_out, or_9_out, or_10_out, or_11_out, or_12_out, or_14_out, or_15_out, or_16_out,
       or_17_out, or_18_out, or_20_out, or_21_out, or_22_out, or_23_out, or_24_out, or_25_out, or_26_out,
       or_28_out, or_29_out, or_30_out, or_31_out, or_32_out, or_33_out, or_35_out, xor_1_out, xor_3_out,
       xor_5_out, xor_7_out, xor_9_out;

  not not_1 (not_1_out, sinal_2);
  not not_2 (not_2_out, sinal);
  not not_3 (not_3_out, or_12_out);
  and and_1 (and_1_out, not_2_out, sinal_2, or_12_out);
  and and_2 (and_2_out, sinal, not_1_out, or_12_out);
  and and_3 (and_3_out, sinal, sinal_2, not_3_out);
  and and_4 (and_4_out, sinal, sinal_2, or_12_out);
  and and_5 (and_5_out, not_2_out, not_1_out, or_12_out);
  and and_6 (and_6_out, not_2_out, sinal_2, not_3_out);
  and and_7 (and_7_out, sinal, not_1_out, not_3_out);
  and and_8 (and_8_out, sinal, sinal_2, or_12_out);
  and and_9 (and_9_out, sinal_4, sinal_3);
  xor xor_1 (xor_1_out, sinal_4, sinal_3);
  Adder #(.width(1)) adder_1 (.a(sinal_6), .b(sinal_5), .out(sinal_9), .cin(adder_2_cout), .cout(adder_1_cout));
  or or_1 (or_1_out, and_1_out, and_2_out);
  or or_2 (or_2_out, and_3_out, and_4_out);
  or or_3 (or_3_out, and_5_out, and_6_out);
  or or_4 (or_4_out, and_7_out, and_8_out);
  or or_5 (or_5_out, and_9_out, and_10_out);
  and and_10 (and_10_out, xor_1_out, or_14_out);
  xor xor_2 (sinal_8, xor_1_out, or_14_out);
  not not_4 (not_4_out, in_2);
  or or_6 (or_6_out, or_1_out, or_2_out);
  or or_7 (sinal_7, or_3_out, or_4_out);
  Adder #(.width(1)) adder_2 (.a(in_27), .b(in_22), .out(out_42), .cin(adder_3_cout), .cout(adder_2_cout));
  not not_5 (not_5_out, in_7);
  not not_6 (not_6_out, or_16_out);
  and and_11 (and_11_out, in_17, in_12);
  xor xor_3 (xor_3_out, in_17, in_12);
  Adder #(.width(1)) adder_3 (.a(in_28), .b(in_23), .out(out_43), .cin(adder_4_cout), .cout(adder_3_cout));
  and and_12 (and_12_out, not_4_out, in_7, or_16_out);
  or or_8 (or_8_out, and_12_out, and_13_out);
  and and_13 (and_13_out, in_2, not_5_out, or_16_out);
  and and_14 (and_14_out, in_2, in_7, not_6_out);
  or or_9 (or_9_out, and_14_out, and_15_out);
  and and_15 (and_15_out, in_2, in_7, or_16_out);
  and and_16 (and_16_out, not_4_out, not_5_out, or_16_out);
  or or_10 (or_10_out, and_16_out, and_17_out);
  and and_17 (and_17_out, not_4_out, in_7, not_6_out);
  and and_18 (and_18_out, in_2, not_5_out, not_6_out);
  or or_11 (or_11_out, and_18_out, and_19_out);
  and and_19 (and_19_out, in_2, in_7, or_16_out);
  and and_20 (and_20_out, xor_3_out, or_21_out);
  xor xor_4 (out_37, xor_3_out, or_21_out);
  or or_12 (or_12_out, or_8_out, or_9_out);
  or or_13 (out_32, or_10_out, or_11_out);
  or or_14 (or_14_out, and_11_out, and_20_out);
  Adder #(.width(1)) adder_4 (.a(in_29), .b(in_24), .out(out_44), .cin(adder_5_cout), .cout(adder_4_cout));
  not not_7 (not_7_out, in_8);
  not not_8 (not_8_out, or_26_out);
  not not_9 (not_9_out, in_3);
  and and_21 (and_21_out, not_9_out, in_8, or_26_out);
  and and_22 (and_22_out, in_3, not_7_out, or_26_out);
  and and_23 (and_23_out, in_3, in_8, not_8_out);
  and and_24 (and_24_out, in_3, in_8, or_26_out);
  and and_25 (and_25_out, not_9_out, not_7_out, or_26_out);
  and and_26 (and_26_out, not_9_out, in_8, not_8_out);
  and and_27 (and_27_out, in_3, not_7_out, not_8_out);
  and and_28 (and_28_out, in_3, in_8, or_26_out);
  and and_29 (and_29_out, in_18, in_13);
  xor xor_5 (xor_5_out, in_18, in_13);
  Adder #(.width(1)) adder_5 (.a(in_30), .b(in_25), .out(out_45), .cin(1'b0), .cout(adder_5_cout));
  or or_15 (or_15_out, and_21_out, and_22_out);
  or or_16 (or_16_out, or_15_out, or_17_out);
  or or_17 (or_17_out, and_23_out, and_24_out);
  or or_18 (or_18_out, and_25_out, and_26_out);
  or or_19 (out_33, or_18_out, or_20_out);
  or or_20 (or_20_out, and_27_out, and_28_out);
  or or_21 (or_21_out, and_29_out, and_30_out);
  and and_30 (and_30_out, xor_5_out, or_28_out);
  xor xor_6 (out_38, xor_5_out, or_28_out);
  not not_10 (not_10_out, in_4);
  not not_11 (not_11_out, in_9);
  not not_12 (not_12_out, or_33_out);
  and and_31 (and_31_out, not_10_out, in_9, or_33_out);
  and and_32 (and_32_out, in_4, not_11_out, or_33_out);
  and and_33 (and_33_out, in_4, in_9, not_12_out);
  and and_34 (and_34_out, in_4, in_9, or_33_out);
  and and_35 (and_35_out, not_10_out, not_11_out, or_33_out);
  and and_36 (and_36_out, not_10_out, in_9, not_12_out);
  and and_37 (and_37_out, in_4, not_11_out, not_12_out);
  and and_38 (and_38_out, in_4, in_9, or_33_out);
  and and_39 (and_39_out, in_19, in_14);
  xor xor_7 (xor_7_out, in_19, in_14);
  or or_22 (or_22_out, and_31_out, and_32_out);
  or or_23 (or_23_out, and_33_out, and_34_out);
  or or_24 (or_24_out, and_35_out, and_36_out);
  or or_25 (or_25_out, and_37_out, and_38_out);
  and and_40 (and_40_out, xor_7_out, or_35_out);
  xor xor_8 (out_39, xor_7_out, or_35_out);
  not not_13 (not_13_out, in_5);
  or or_26 (or_26_out, or_22_out, or_23_out);
  or or_27 (out_34, or_24_out, or_25_out);
  or or_28 (or_28_out, and_39_out, and_40_out);
  not not_14 (not_14_out, 1'b0);
  not not_15 (not_15_out, in_10);
  and and_41 (and_41_out, in_20, in_15);
  xor xor_9 (xor_9_out, in_20, in_15);
  and and_42 (and_42_out, not_13_out, in_10, 1'b0);
  or or_29 (or_29_out, and_42_out, and_43_out);
  and and_43 (and_43_out, in_5, not_15_out, 1'b0);
  and and_44 (and_44_out, in_5, in_10, not_14_out);
  or or_30 (or_30_out, and_44_out, and_45_out);
  and and_45 (and_45_out, in_5, in_10, 1'b0);
  and and_46 (and_46_out, not_13_out, not_15_out, 1'b0);
  or or_31 (or_31_out, and_46_out, and_47_out);
  and and_47 (and_47_out, not_13_out, in_10, not_14_out);
  and and_48 (and_48_out, in_5, not_15_out, not_14_out);
  or or_32 (or_32_out, and_48_out, and_49_out);
  and and_49 (and_49_out, in_5, in_10, 1'b0);
  and and_50 (and_50_out, xor_9_out, 1'b0);
  xor xor_10 (out_40, xor_9_out, 1'b0);
  or or_33 (or_33_out, or_29_out, or_30_out);
  or or_34 (out_35, or_31_out, or_32_out);
  or or_35 (or_35_out, and_41_out, and_50_out);
  // also tied to GND on the sheet: {adder_1_cout, or_5_out, or_6_out}

  // Notes on the sheet:
  //   descartado
  //   descartado
  //   SOMADOR 5 BITS NATIVO
  //   SOMADOR 5 BITS AND/OR
  //   SOMADOR 5 BITS SIMPLIFICADO
  //   0 arbitrario
  //   0 arbitrario
endmodule
