// Logisim project exemplo0802.circ as structural Verilog: 1 circuit, main circuit main
module main (
  input  sinal,
  input  in_2,
  input  in_3,
  input  in_4,
  input  in_5,
  input  sinal_2,
  input  in_7,
  input  in_8,
  input  in_9,
  input  in_10,
  input  sinal_3,
  input  in_12,
  input  in_13,
  input  in_14,
  input  in_15,
  input  sinal_4,
  input  in_17,
  input  in_18,
  input  in_19,
  input  in_20,
  output sinal_5,
  output out_22,
  output out_23,
  output out_24,
  output out_25,
  output sinal_6,
  output out_27,
  output out_28,
  output out_29,
  output out_30
);

  wire and_1_out, and_2_out, and_3_out, and_4_out, and_5_out, and_6_out, and_7_out, and_8_out, and_9_out,
       and_10_out, not_1_out, not_2_out, not_3_out, not_4_out, not_5_out, not_6_out, not_7_out, not_8_out,
       not_9_out, not_10_out, or_1_out, or_2_out, or_3_out, or_4_out, or_5_out, subtractor_1_bout,
       subtractor_2_bout, subtractor_3_bout, subtractor_4_bout, subtractor_5_bout, xor_1_out, xor_3_out,
       xor_5_out, xor_7_out, xor_9_out;

  and and_1 (and_1_out, sinal_2, not_1_out);
  not not_1 (not_1_out, sinal);
  xor xor_1 (xor_1_out, sinal_2, sinal);
  Subtractor #(.width(1)) subtractor_1 (
    .a(sinal_3), .b(sinal_4), .out(sinal_6), .bin(subtractor_2_bout), .bout(subtractor_1_bout));
  not not_2 (not_2_out, xor_1_out);
  and and_2 (and_2_out, not_2_out, or_2_out);
  xor xor_2 (sinal_5, xor_1_out, or_2_out);
  or or_1 (or_1_out, and_1_out, and_2_out);
  Subtractor #(.width(1)) subtractor_2 (
    .a(in_12), .b(in_17), .out(out_27), .bin(subtractor_3_bout), .bout(subtractor_2_bout));
  and and_3 (and_3_out, in_7, not_3_out);
  not not_3 (not_3_out, in_2);
  xor xor_3 (xor_3_out, in_7, in_2);
  Subtractor #(.width(1)) subtractor_3 (
    .a(in_13), .b(in_18), .out(out_28), .bin(subtractor_4_bout), .bout(subtractor_3_bout));
  not not_4 (not_4_out, xor_3_out);
  and and_4 (and_4_out, not_4_out, or_3_out);
  xor xor_4 (out_22, xor_3_out, or_3_out);
  or or_2 (or_2_out, and_3_out, and_4_out);
  Subtractor #(.width(1)) subtractor_4 (
    .a(in_14), .b(in_19), .out(out_29), .bin(subtractor_5_bout), .bout(subtractor_4_bout));
  not not_5 (not_5_out, in_3);
  and and_5 (and_5_out, in_8, not_5_out);
  not not_6 (not_6_out, xor_5_out);
  xor xor_5 (xor_5_out, in_8, in_3);
  Subtractor #(.width(1)) subtractor_5 (.a(in_15), .b(in_20), .out(out_30), .bin(1'b0), .bout(subtractor_5_bout));
  or or_3 (or_3_out, and_5_out, and_6_out);
  and and_6 (and_6_out, not_6_out, or_4_out);
  xor xor_6 (out_23, xor_5_out, or_4_out);
  and and_7 (and_7_out, in_9, not_7_out);
  not not_7 (not_7_out, in_4);
  xor xor_7 (xor_7_out, in_9, in_4);
  not not_8 (not_8_out, xor_7_out);
  and and_8 (and_8_out, not_8_out, or_5_out);
  xor xor_8 (out_24, xor_7_out, or_5_out);
  or or_4 (or_4_out, and_7_out, and_8_out);
  and and_9 (and_9_out, in_10, not_9_out);
  not not_9 (not_9_out, in_5);
  xor xor_9 (xor_9_out, in_10, in_5);
  not not_10 (not_10_out, xor_9_out);
  and and_10 (and_10_out, not_10_out, 1'b0);
  xor xor_10 (out_25, xor_9_out, 1'b0);
  or or_5 (or_5_out, and_9_out, and_10_out);
  // also tied to GND on the sheet: {subtractor_1_bout, or_1_out}

  // Notes on the sheet:
  //   descartado
  //   SUBTRATOR 5 BITS NATIVO
  //   SUBTRATOR 5 BITS SIMPLIFICADO
  //   0 arbitrario
endmodule
