// Logisim project exemplo0803.circ as structural Verilog: 1 circuit, main circuit main
module main (
  input  sinal,
  input  in_2,
  input  in_3,
  input  in_4,
  input  in_5,
  input  sinal_2,
  input  in_7,
  input  in_8,
  input  in_9,
  input  in_10,
  output out_11
);

  wire xnor_1_out, xnor_2_out, xnor_3_out, xnor_4_out, xnor_5_out;

  xnor xnor_1 (xnor_1_out, sinal, sinal_2);
  xnor xnor_2 (xnor_2_out, in_2, in_7);
  xnor xnor_3 (xnor_3_out, in_4, in_9);
  xnor xnor_4 (xnor_4_out, in_3, in_8);
  and and_1 (out_11, xnor_1_out, xnor_2_out, xnor_4_out, xnor_3_out, xnor_5_out);
  xnor xnor_5 (xnor_5_out, in_5, in_10);

  // Notes on the sheet:
  //   COMPARADOR 5 BITS SIMPLIFICADO
endmodule
