// Logisim project exemplo0804.circ as structural Verilog: 1 circuit, main circuit main
module main (
  input  sinal,
  input  in_2,
  input  in_3,
  input  in_4,
  input  in_5,
  input  sinal_2,
  input  in_7,
  input  in_8,
  input  in_9,
  input  in_10,
  output out_11
);

  wire xor_1_out, xor_2_out, xor_3_out, xor_4_out, xor_5_out;

  xor xor_1 (xor_1_out, in_2, in_7);
  xor xor_2 (xor_2_out, sinal, sinal_2);
  xor xor_3 (xor_3_out, in_4, in_9);
  xor xor_4 (xor_4_out, in_3, in_8);
  or or_1 (out_11, xor_2_out, xor_1_out, xor_4_out, xor_3_out, xor_5_out);
  xor xor_5 (xor_5_out, in_5, in_10);

  // Notes on the sheet:
  //   COMPARADOR DE DESIGUALDADE DE 5 BITS SIMPLIFICADO
endmodule
