// Logisim project exemplo0805.circ as structural Verilog: 1 circuit, main circuit main
module main (
  input  sinal,
  input  in_2,
  input  in_3,
  input  in_4,
  input  in_5,
  output out_6,
  output out_7,
  output out_8,
  output out_9,
  output out_10
);

  wire and_1_out, and_2_out, and_3_out, and_4_out, and_5_out, not_1_out, not_2_out, not_3_out, not_4_out,
       not_5_out;

  not not_1 (not_1_out, sinal);
  and and_1 (and_1_out, not_1_out, and_2_out);
  xor xor_1 (out_6, not_1_out, and_2_out);
  not not_2 (not_2_out, in_2);
  and and_2 (and_2_out, not_2_out, and_3_out);
  xor xor_2 (out_7, not_2_out, and_3_out);
  not not_3 (not_3_out, in_3);
  and and_3 (and_3_out, not_3_out, and_4_out);
  xor xor_3 (out_8, not_3_out, and_4_out);
  not not_4 (not_4_out, in_4);
  and and_4 (and_4_out, not_4_out, and_5_out);
  xor xor_4 (out_9, not_4_out, and_5_out);
  not not_5 (not_5_out, in_5);
  and and_5 (and_5_out, not_5_out, 1'b1);
  xor xor_5 (out_10, not_5_out, 1'b1);
  // also tied to GND on the sheet: and_1_out

  // Notes on the sheet:
  //   descartado
  //   COMPLEMENTO DE 2 SIMPLIFICADO
  //   0 arbitrario
endmodule
