// Logisim project questao_02_moore.circ as structural Verilog: 1 circuit, main circuit main
module main (
  input  pulso,
  input  clr,
  output out_3
);

  wire CLK_out, d_ff_1_q, d_ff_2_q, d_ff_3_q, d_ff_3_qn, d_ff_4_q, d_ff_5_q;

  Clock CLK (.out(CLK_out));
  D_Flip_Flop d_ff_1 (.clk(CLK_out), .D(pulso), .Q(d_ff_1_q), .reset(clr));  // open: Qn, preset
  D_Flip_Flop d_ff_2 (.clk(CLK_out), .D(d_ff_1_q), .Q(d_ff_2_q), .reset(clr));  // open: Qn, preset
  and and_1 (out_3, d_ff_5_q, d_ff_4_q, d_ff_3_qn, d_ff_2_q);
  D_Flip_Flop d_ff_3 (.clk(CLK_out), .D(d_ff_2_q), .Q(d_ff_3_q), .Qn(d_ff_3_qn), .reset(clr));  // open: preset
  D_Flip_Flop d_ff_4 (.clk(CLK_out), .D(d_ff_3_q), .Q(d_ff_4_q), .reset(clr));  // open: Qn, preset
  D_Flip_Flop d_ff_5 (.clk(CLK_out), .D(d_ff_4_q), .Q(d_ff_5_q), .reset(clr));  // open: Qn, preset
endmodule
