// Logisim project questao_03_mealy_e_moore.circ as structural Verilog: 1 circuit, main circuit main
module main (
  input  Input,
  input  Clear,
  output mealy,
  output moore
);

  wire Clock_out, d_ff_1_q, d_ff_2_q, d_ff_3_q, d_ff_4_q, d_ff_4_qn, d_ff_5_q, d_ff_5_qn, d_ff_6_q, d_ff_7_q,
       d_ff_8_q, d_ff_9_q;

  Clock Clock (.out(Clock_out));
  D_Flip_Flop d_ff_1 (.clk(Clock_out), .D(Input), .Q(d_ff_1_q), .reset(Clear));  // open: Qn, preset
  D_Flip_Flop d_ff_2 (.clk(Clock_out), .D(Input), .Q(d_ff_2_q), .reset(Clear));  // open: Qn, preset
  D_Flip_Flop d_ff_3 (.clk(Clock_out), .D(d_ff_1_q), .Q(d_ff_3_q), .reset(Clear));  // open: Qn, preset
  D_Flip_Flop d_ff_4 (.clk(Clock_out), .D(d_ff_2_q), .Q(d_ff_4_q), .Qn(d_ff_4_qn), .reset(Clear));  // open: preset
  D_Flip_Flop d_ff_5 (.clk(Clock_out), .D(d_ff_3_q), .Q(d_ff_5_q), .Qn(d_ff_5_qn), .reset(Clear));  // open: preset
  D_Flip_Flop d_ff_6 (.clk(Clock_out), .D(d_ff_4_q), .Q(d_ff_6_q), .reset(Clear));  // open: Qn, preset
  D_Flip_Flop d_ff_7 (.clk(Clock_out), .D(d_ff_5_q), .Q(d_ff_7_q), .reset(Clear));  // open: Qn, preset
  D_Flip_Flop d_ff_8 (.clk(Clock_out), .D(d_ff_6_q), .Q(d_ff_8_q), .reset(Clear));  // open: Qn, preset
  D_Flip_Flop d_ff_9 (.clk(Clock_out), .D(d_ff_7_q), .Q(d_ff_9_q), .reset(Clear));  // open: Qn, preset
  and and_1 (mealy, d_ff_8_q, d_ff_6_q, d_ff_4_qn, d_ff_2_q);
  and and_2 (moore, d_ff_9_q, d_ff_7_q, d_ff_5_qn, d_ff_3_q);
endmodule
