// Logisim project questao_05_1011_duas_vezes.circ as structural Verilog: 1 circuit, main circuit main
module main (
  input  Input,
  input  Clear,
  output out_3
);

  wire and_1_out, and_2_out, and_3_out, and_4_out, and_5_out, and_6_out, Clock_out, d_ff_1_q, d_ff_2_q,
       d_ff_3_q, d_ff_3_qn, d_ff_4_q, demultiplexer_1_out0, demultiplexer_1_out1, not_1_out, not_2_out,
       not_3_out, or_1_out, or_2_out, or_3_out, or_4_out, or_5_out, or_6_out;

  Clock Clock (.out(Clock_out));
  D_Flip_Flop d_ff_1 (.clk(Clock_out), .D(Input), .Q(d_ff_1_q), .reset(or_1_out));  // open: Qn, preset
  or or_1 (or_1_out, or_6_out, Clear);
  D_Flip_Flop d_ff_2 (.clk(Clock_out), .D(d_ff_1_q), .Q(d_ff_2_q), .reset(or_2_out));  // open: Qn, preset
  or or_2 (or_2_out, or_6_out, Clear);
  or or_3 (or_3_out, or_6_out, Clear);
  D_Flip_Flop d_ff_3 (.clk(Clock_out), .D(d_ff_2_q), .Q(d_ff_3_q), .Qn(d_ff_3_qn), .reset(or_3_out));  // open: preset
  or or_4 (or_4_out, or_6_out, Clear);
  D_Flip_Flop d_ff_4 (.clk(Clock_out), .D(d_ff_3_q), .Q(d_ff_4_q), .reset(or_4_out));  // open: Qn, preset
  not not_1 (not_1_out, Clock_out);
  not not_2 (not_2_out, not_1_out);
  and and_1 (and_1_out, not_1_out, and_2_out);
  and and_2 (and_2_out, d_ff_4_q, d_ff_3_qn, d_ff_2_q, d_ff_1_q);
  Demultiplexer #(.enable("false")) demultiplexer_1 (
    .out0(demultiplexer_1_out0), .out1(demultiplexer_1_out1), .in(and_1_out), .sel(or_5_out));
  or or_5 (or_5_out, and_3_out, and_4_out);
  and and_3 (and_3_out, not_2_out, demultiplexer_1_out0);
  and and_4 (and_4_out, or_5_out, not_3_out);
  not not_3 (not_3_out, Clear);
  and and_5 (and_5_out, not_3_out, or_6_out);
  and and_6 (and_6_out, or_5_out, demultiplexer_1_out1);
  or or_6 (or_6_out, and_5_out, and_6_out);
  and and_7 (out_3, or_5_out, or_6_out);

  // Notes on the sheet:
  //   Ative o Clear antes de comecar para retirar o bug
endmodule
