// Logisim project questao_06_1011_tres_vezes.circ as structural Verilog: 1 circuit, main circuit main
module main (
  input  Input,
  input  Clear,
  output out_3
);

  wire and_1_out, Clock_out, d_ff_1_q, d_ff_2_q, d_ff_3_q, d_ff_3_qn, d_ff_4_q, not_1_out, or_1_out,
       or_2_out, or_3_out, or_4_out;

  Clock Clock (.out(Clock_out));
  D_Flip_Flop d_ff_1 (.clk(Clock_out), .D(Input), .Q(d_ff_1_q), .reset(or_1_out));  // open: Qn, preset
  or or_1 (or_1_out, out_3, Clear);
  D_Flip_Flop d_ff_2 (.clk(Clock_out), .D(d_ff_1_q), .Q(d_ff_2_q), .reset(or_2_out));  // open: Qn, preset
  or or_2 (or_2_out, out_3, Clear);
  or or_3 (or_3_out, out_3, Clear);
  D_Flip_Flop d_ff_3 (.clk(Clock_out), .D(d_ff_2_q), .Q(d_ff_3_q), .Qn(d_ff_3_qn), .reset(or_3_out));  // open: preset
  or or_4 (or_4_out, out_3, Clear);
  D_Flip_Flop d_ff_4 (.clk(Clock_out), .D(d_ff_3_q), .Q(d_ff_4_q), .reset(or_4_out));  // open: Qn, preset
  and and_1 (and_1_out, d_ff_4_q, d_ff_3_qn, d_ff_2_q, d_ff_1_q);
  not not_1 (not_1_out, out_3);
  Counter #(.width(2), .max('h3)) counter_1 (
    .count(not_1_out), .carry(out_3), .clk(and_1_out), .clr(Clear));  // open: load, D, Q, preset, down
endmodule
