// Logisim project logisim.circ as structural Verilog: 9 circuits, main circuit RAM 1X4
module RAM_1X4 (
  input  [3:0] Input,
  input  Clock,
  input  Read_Write,
  input  Address,
  input  Clear,
  output [3:0] Output
);

  wire and_1_out, j_k_ff_1_q, j_k_ff_2_q, j_k_ff_3_q, j_k_ff_4_q, not_1_out, not_2_out, not_3_out, not_4_out;

  and and_1 (and_1_out, Clock, Read_Write, Address);
  J_K_Flip_Flop j_k_ff_1 (
    .J(Input[0]), .clk(and_1_out), .K(not_1_out), .Q(j_k_ff_1_q), .reset(Clear));  // open: Qn, preset
  not not_1 (not_1_out, Input[0]);
  and and_2 (Output[0], Address, j_k_ff_1_q);
  not not_2 (not_2_out, Input[1]);
  J_K_Flip_Flop j_k_ff_2 (
    .J(Input[1]), .clk(and_1_out), .K(not_2_out), .Q(j_k_ff_2_q), .reset(Clear));  // open: Qn, preset
  not not_3 (not_3_out, Input[2]);
  and and_3 (Output[1], Address, j_k_ff_2_q);
  J_K_Flip_Flop j_k_ff_3 (
    .J(Input[2]), .clk(and_1_out), .K(not_3_out), .Q(j_k_ff_3_q), .reset(Clear));  // open: Qn, preset
  not not_4 (not_4_out, Input[3]);
  and and_4 (Output[2], Address, j_k_ff_3_q);
  J_K_Flip_Flop j_k_ff_4 (
    .J(Input[3]), .clk(and_1_out), .K(not_4_out), .Q(j_k_ff_4_q), .reset(Clear));  // open: Qn, preset
  and and_5 (Output[3], Address, j_k_ff_4_q);
endmodule

module RAM_1X2 (
  input  [1:0] Input,
  input  Clock,
  input  Read_Write,
  input  Address,
  input  Clear,
  output [1:0] Output
);

  wire and_1_out, j_k_ff_1_q, j_k_ff_2_q, not_1_out, not_2_out;

  and and_1 (and_1_out, Clock, Read_Write, Address);
  J_K_Flip_Flop j_k_ff_1 (
    .J(Input[0]), .clk(and_1_out), .K(not_1_out), .Q(j_k_ff_1_q), .reset(Clear));  // open: Qn, preset
  not not_1 (not_1_out, Input[0]);
  and and_2 (Output[0], Address, j_k_ff_1_q);
  not not_2 (not_2_out, Input[1]);
  J_K_Flip_Flop j_k_ff_2 (
    .J(Input[1]), .clk(and_1_out), .K(not_2_out), .Q(j_k_ff_2_q), .reset(Clear));  // open: Qn, preset
  and and_3 (Output[1], Address, j_k_ff_2_q);
endmodule

module RAM_1X4__2x_1x2 (
  input  [3:0] Input,
  input  Clock,
  input  Read_Write,
  input  Address,
  input  Clear,
  output [3:0] Output
);

  RAM_1X2 ram_1x2_1 (
    .Clock(Clock), .Read_Write(Read_Write), .Address(Address), .Input(Input[1:0]), .Output(Output[1:0]),
    .Clear(Clear));
  RAM_1X2 ram_1x2_2 (
    .Clock(Clock), .Read_Write(Read_Write), .Address(Address), .Input(Input[3:2]), .Output(Output[3:2]),
    .Clear(Clear));
endmodule

module RAM_2X4 (
  input  [3:0] Input,
  input  Clock,
  input  Read_Write,
  input  Address,
  input  Clear,
  output [3:0] Output
);

  wire demultiplexer_1_out0, demultiplexer_1_out1;
  wire [3:0] ram_1x4_2x_1x2_1_output, ram_1x4_2x_1x2_2_output;

  Demultiplexer #(.enable("false")) demultiplexer_1 (
    .out0(demultiplexer_1_out0), .out1(demultiplexer_1_out1), .in(1'b1), .sel(Address));
  RAM_1X4__2x_1x2 ram_1x4_2x_1x2_1 (
    .Clock(Clock), .Read_Write(Read_Write), .Address(demultiplexer_1_out0), .Clear(Clear), .Input(Input),
    .Output(ram_1x4_2x_1x2_1_output));
  RAM_1X4__2x_1x2 ram_1x4_2x_1x2_2 (
    .Clock(Clock), .Read_Write(Read_Write), .Address(demultiplexer_1_out1), .Clear(Clear), .Input(Input),
    .Output(ram_1x4_2x_1x2_2_output));
  Multiplexer #(.width(4), .enable("false")) multiplexer_1 (
    .in0(ram_1x4_2x_1x2_1_output), .in1(ram_1x4_2x_1x2_2_output), .out(Output), .sel(Address));
endmodule

module RAM_4X8 (
  input  Clock,
  input  [7:0] Input,
  input  Read_Write,
  input  [1:0] Address,
  input  Clear,
  output [7:0] Output
);

  wire and_1_out, and_2_out, demultiplexer_1_out0, demultiplexer_1_out1, demultiplexer_1_out2,
       demultiplexer_1_out3, or_1_out, or_2_out;
  wire [3:0] ram_2x4_1_output, ram_2x4_2_output, ram_2x4_3_output, ram_2x4_4_output;

  Demultiplexer #(.select(2), .enable("false")) demultiplexer_1 (
    .out0(demultiplexer_1_out0), .out1(demultiplexer_1_out1), .out2(demultiplexer_1_out2),
    .out3(demultiplexer_1_out3), .in(1'b1), .sel(Address));
  and and_1 (and_1_out, Read_Write, or_1_out);
  or or_1 (or_1_out, demultiplexer_1_out0, demultiplexer_1_out1);
  RAM_2X4 ram_2x4_1 (
    .Clock(Clock), .Read_Write(and_1_out), .Address(demultiplexer_1_out1), .Clear(Clear), .Input(Input[7:4]),
    .Output(ram_2x4_1_output));
  RAM_2X4 ram_2x4_2 (
    .Clock(Clock), .Read_Write(and_1_out), .Address(demultiplexer_1_out1), .Clear(Clear), .Input(Input[3:0]),
    .Output(ram_2x4_2_output));
  and and_2 (and_2_out, Read_Write, or_2_out);
  or or_2 (or_2_out, demultiplexer_1_out2, demultiplexer_1_out3);
  RAM_2X4 ram_2x4_3 (
    .Clock(Clock), .Read_Write(and_2_out), .Address(demultiplexer_1_out3), .Clear(Clear), .Input(Input[7:4]),
    .Output(ram_2x4_3_output));
  Multiplexer #(.select(2), .width(4), .enable("false")) multiplexer_1 (
    .in0(ram_2x4_2_output), .in1(ram_2x4_2_output), .in2(ram_2x4_4_output), .in3(ram_2x4_4_output),
    .out(Output[3:0]), .sel(Address));
  RAM_2X4 ram_2x4_4 (
    .Clock(Clock), .Read_Write(and_2_out), .Address(demultiplexer_1_out3), .Clear(Clear), .Input(Input[3:0]),
    .Output(ram_2x4_4_output));
  Multiplexer #(.select(2), .width(4), .enable("false")) multiplexer_2 (
    .in0(ram_2x4_1_output), .in1(ram_2x4_1_output), .in2(ram_2x4_3_output), .in3(ram_2x4_3_output),
    .out(Output[7:4]), .sel(Address));
endmodule

module RAM_8X8 (
  input  [7:0] Input,
  input  Clock,
  input  Read_Write,
  input  [2:0] in_4,
  input  Clear,
  output [7:0] Output
);

  wire and_1_out, and_2_out, demultiplexer_1_out0, demultiplexer_1_out1, demultiplexer_1_out2,
       demultiplexer_1_out3, demultiplexer_1_out4, demultiplexer_1_out5, demultiplexer_1_out6,
       demultiplexer_1_out7, priority_encoder_1_gs, priority_encoder_2_gs;
  wire [1:0] priority_encoder_1_out, priority_encoder_2_out;
  wire [7:0] ram_4x8_1_output, ram_4x8_2_output;

  Demultiplexer #(.select(3), .enable("false")) demultiplexer_1 (
    .out0(demultiplexer_1_out0), .out1(demultiplexer_1_out1), .out2(demultiplexer_1_out2),
    .out3(demultiplexer_1_out3), .out4(demultiplexer_1_out4), .out5(demultiplexer_1_out5),
    .out6(demultiplexer_1_out6), .out7(demultiplexer_1_out7), .in(1'b1), .sel(in_4));
  and and_1 (and_1_out, Read_Write, priority_encoder_1_gs);
  Priority_Encoder #(.select(2)) priority_encoder_1 (
    .in0(demultiplexer_1_out0), .in1(demultiplexer_1_out1), .in2(demultiplexer_1_out2),
    .in3(demultiplexer_1_out3), .out(priority_encoder_1_out), .gs(priority_encoder_1_gs));  // open: en_out, en_in
  RAM_4X8 ram_4x8_1 (
    .Clock(Clock), .Read_Write(and_1_out), .Address(priority_encoder_1_out), .Clear(Clear), .Input(Input),
    .Output(ram_4x8_1_output));
  Priority_Encoder #(.select(2)) priority_encoder_2 (
    .in0(demultiplexer_1_out4), .in1(demultiplexer_1_out5), .in2(demultiplexer_1_out6),
    .in3(demultiplexer_1_out7), .out(priority_encoder_2_out), .gs(priority_encoder_2_gs));  // open: en_out, en_in
  and and_2 (and_2_out, Read_Write, priority_encoder_2_gs);
  RAM_4X8 ram_4x8_2 (
    .Clock(Clock), .Read_Write(and_2_out), .Address(priority_encoder_2_out), .Clear(Clear), .Input(Input),
    .Output(ram_4x8_2_output));
  Multiplexer #(.width(8), .enable("false")) multiplexer_1 (
    .in0(ram_4x8_1_output), .in1(ram_4x8_2_output), .out(Output), .sel(in_4[2]));
endmodule

module RAM_4X16 (
  input  [15:0] Input,
  input  Clock,
  input  Read_Write,
  input  [1:0] Address,
  input  Clear,
  output [15:0] Output
);

  RAM_4X8 ram_4x8_1 (
    .Clock(Clock), .Read_Write(Read_Write), .Address(Address), .Clear(Clear), .Input(Input[7:0]),
    .Output(Output[7:0]));
  RAM_4X8 ram_4x8_2 (
    .Clock(Clock), .Read_Write(Read_Write), .Address(Address), .Clear(Clear), .Input(Input[15:8]),
    .Output(Output[15:8]));
endmodule

module RAM_1X16 (
  input  [15:0] Input,
  input  Clock,
  input  Read_Write,
  input  Address,
  input  Clear,
  output [15:0] Output
);

  wire and_1_out, j_k_ff_1_q, j_k_ff_2_q, j_k_ff_3_q, j_k_ff_4_q, j_k_ff_5_q, j_k_ff_6_q, j_k_ff_7_q,
       j_k_ff_8_q, j_k_ff_9_q, j_k_ff_10_q, j_k_ff_11_q, j_k_ff_12_q, j_k_ff_13_q, j_k_ff_14_q, j_k_ff_15_q,
       j_k_ff_16_q, not_1_out, not_2_out, not_3_out, not_4_out, not_5_out, not_6_out, not_7_out, not_8_out,
       not_9_out, not_10_out, not_11_out, not_12_out, not_13_out, not_14_out, not_15_out, not_16_out;

  and and_1 (and_1_out, Clock, Read_Write, Address);
  J_K_Flip_Flop j_k_ff_1 (
    .J(Input[0]), .clk(and_1_out), .K(not_1_out), .Q(j_k_ff_1_q), .reset(Clear));  // open: Qn, preset
  not not_1 (not_1_out, Input[0]);
  and and_2 (Output[0], Address, j_k_ff_1_q);
  not not_2 (not_2_out, Input[1]);
  J_K_Flip_Flop j_k_ff_2 (
    .J(Input[1]), .clk(and_1_out), .K(not_2_out), .Q(j_k_ff_2_q), .reset(Clear));  // open: Qn, preset
  not not_3 (not_3_out, Input[2]);
  and and_3 (Output[1], Address, j_k_ff_2_q);
  J_K_Flip_Flop j_k_ff_3 (
    .J(Input[2]), .clk(and_1_out), .K(not_3_out), .Q(j_k_ff_3_q), .reset(Clear));  // open: Qn, preset
  not not_4 (not_4_out, Input[3]);
  and and_4 (Output[2], Address, j_k_ff_3_q);
  J_K_Flip_Flop j_k_ff_4 (
    .J(Input[3]), .clk(and_1_out), .K(not_4_out), .Q(j_k_ff_4_q), .reset(Clear));  // open: Qn, preset
  and and_5 (Output[3], Address, j_k_ff_4_q);
  J_K_Flip_Flop j_k_ff_5 (
    .J(Input[4]), .clk(and_1_out), .K(not_5_out), .Q(j_k_ff_5_q), .reset(Clear));  // open: Qn, preset
  not not_5 (not_5_out, Input[4]);
  and and_6 (Output[4], Address, j_k_ff_5_q);
  not not_6 (not_6_out, Input[5]);
  J_K_Flip_Flop j_k_ff_6 (
    .J(Input[5]), .clk(and_1_out), .K(not_6_out), .Q(j_k_ff_6_q), .reset(Clear));  // open: Qn, preset
  not not_7 (not_7_out, Input[6]);
  and and_7 (Output[5], Address, j_k_ff_6_q);
  J_K_Flip_Flop j_k_ff_7 (
    .J(Input[6]), .clk(and_1_out), .K(not_7_out), .Q(j_k_ff_7_q), .reset(Clear));  // open: Qn, preset
  not not_8 (not_8_out, Input[7]);
  and and_8 (Output[6], Address, j_k_ff_7_q);
  J_K_Flip_Flop j_k_ff_8 (
    .J(Input[7]), .clk(and_1_out), .K(not_8_out), .Q(j_k_ff_8_q), .reset(Clear));  // open: Qn, preset
  and and_9 (Output[7], Address, j_k_ff_8_q);
  J_K_Flip_Flop j_k_ff_9 (
    .J(Input[8]), .clk(and_1_out), .K(not_9_out), .Q(j_k_ff_9_q), .reset(Clear));  // open: Qn, preset
  not not_9 (not_9_out, Input[8]);
  and and_10 (Output[8], Address, j_k_ff_9_q);
  not not_10 (not_10_out, Input[9]);
  J_K_Flip_Flop j_k_ff_10 (
    .J(Input[9]), .clk(and_1_out), .K(not_10_out), .Q(j_k_ff_10_q), .reset(Clear));  // open: Qn, preset
  not not_11 (not_11_out, Input[10]);
  and and_11 (Output[9], Address, j_k_ff_10_q);
  J_K_Flip_Flop j_k_ff_11 (
    .J(Input[10]), .clk(and_1_out), .K(not_11_out), .Q(j_k_ff_11_q), .reset(Clear));  // open: Qn, preset
  not not_12 (not_12_out, Input[11]);
  and and_12 (Output[10], Address, j_k_ff_11_q);
  J_K_Flip_Flop j_k_ff_12 (
    .J(Input[11]), .clk(and_1_out), .K(not_12_out), .Q(j_k_ff_12_q), .reset(Clear));  // open: Qn, preset
  and and_13 (Output[11], Address, j_k_ff_12_q);
  J_K_Flip_Flop j_k_ff_13 (
    .J(Input[12]), .clk(and_1_out), .K(not_13_out), .Q(j_k_ff_13_q), .reset(Clear));  // open: Qn, preset
  not not_13 (not_13_out, Input[12]);
  and and_14 (Output[12], Address, j_k_ff_13_q);
  not not_14 (not_14_out, Input[13]);
  J_K_Flip_Flop j_k_ff_14 (
    .J(Input[13]), .clk(and_1_out), .K(not_14_out), .Q(j_k_ff_14_q), .reset(Clear));  // open: Qn, preset
  not not_15 (not_15_out, Input[14]);
  and and_15 (Output[13], Address, j_k_ff_14_q);
  J_K_Flip_Flop j_k_ff_15 (
    .J(Input[14]), .clk(and_1_out), .K(not_15_out), .Q(j_k_ff_15_q), .reset(Clear));  // open: Qn, preset
  not not_16 (not_16_out, Input[15]);
  and and_16 (Output[14], Address, j_k_ff_15_q);
  J_K_Flip_Flop j_k_ff_16 (
    .J(Input[15]), .clk(and_1_out), .K(not_16_out), .Q(j_k_ff_16_q), .reset(Clear));  // open: Qn, preset
  and and_17 (Output[15], Address, j_k_ff_16_q);
endmodule

module RAM_8X16 (
  input  [15:0] Input,
  input  Clock,
  input  Read_Write,
  input  [2:0] Address,
  input  Clear,
  output [15:0] out_6
);

  wire demultiplexer_1_out0, demultiplexer_1_out1, demultiplexer_1_out2, demultiplexer_1_out3,
       demultiplexer_1_out4, demultiplexer_1_out5, demultiplexer_1_out6, demultiplexer_1_out7;
  wire [15:0] ram_1x16_1_output, ram_1x16_2_output, ram_1x16_3_output, ram_1x16_4_output, ram_1x16_5_output,
       ram_1x16_6_output, ram_1x16_7_output, ram_1x16_8_output;

  Demultiplexer #(.select(3), .enable("false")) demultiplexer_1 (
    .out0(demultiplexer_1_out0), .out1(demultiplexer_1_out1), .out2(demultiplexer_1_out2),
    .out3(demultiplexer_1_out3), .out4(demultiplexer_1_out4), .out5(demultiplexer_1_out5),
    .out6(demultiplexer_1_out6), .out7(demultiplexer_1_out7), .in(1'b1), .sel(Address));
  RAM_1X16 ram_1x16_1 (
    .Clock(Clock), .Read_Write(Read_Write), .Address(demultiplexer_1_out0), .Clear(Clear), .Input(Input),
    .Output(ram_1x16_1_output));
  RAM_1X16 ram_1x16_2 (
    .Clock(Clock), .Read_Write(Read_Write), .Address(demultiplexer_1_out1), .Clear(Clear), .Input(Input),
    .Output(ram_1x16_2_output));
  RAM_1X16 ram_1x16_3 (
    .Clock(Clock), .Read_Write(Read_Write), .Address(demultiplexer_1_out2), .Clear(Clear), .Input(Input),
    .Output(ram_1x16_3_output));
  RAM_1X16 ram_1x16_4 (
    .Clock(Clock), .Read_Write(Read_Write), .Address(demultiplexer_1_out3), .Clear(Clear), .Input(Input),
    .Output(ram_1x16_4_output));
  RAM_1X16 ram_1x16_5 (
    .Clock(Clock), .Read_Write(Read_Write), .Address(demultiplexer_1_out4), .Clear(Clear), .Input(Input),
    .Output(ram_1x16_5_output));
  RAM_1X16 ram_1x16_6 (
    .Clock(Clock), .Read_Write(Read_Write), .Address(demultiplexer_1_out5), .Clear(Clear), .Input(Input),
    .Output(ram_1x16_6_output));
  RAM_1X16 ram_1x16_7 (
    .Clock(Clock), .Read_Write(Read_Write), .Address(demultiplexer_1_out6), .Clear(Clear), .Input(Input),
    .Output(ram_1x16_7_output));
  RAM_1X16 ram_1x16_8 (
    .Clock(Clock), .Read_Write(Read_Write), .Address(demultiplexer_1_out7), .Clear(Clear), .Input(Input),
    .Output(ram_1x16_8_output));
  Multiplexer #(.select(3), .width(16), .enable("false")) multiplexer_1 (
    .in0(ram_1x16_1_output), .in1(ram_1x16_2_output), .in2(ram_1x16_3_output), .in3(ram_1x16_4_output),
    .in4(ram_1x16_5_output), .in5(ram_1x16_6_output), .in6(ram_1x16_7_output), .in7(ram_1x16_8_output),
    .out(out_6), .sel(Address));
endmodule
