// Logisim project logisim.circ as structural Verilog: 7 circuits, main circuit Contador Decrescente (6bits)
module Contador_Decrescente__6bits (
  output out_1,
  output out_2,
  output out_3,
  output out_4,
  output out_5,
  output out_6
);

  wire Clear_out, pulse_out;

  Button pulse (.out(pulse_out));
  Button Clear (.out(Clear_out));
  J_K_Flip_Flop j_k_ff_1 (.J(1'b1), .clk(out_2), .K(1'b1), .Qn(out_1), .reset(Clear_out));  // open: Q, preset
  J_K_Flip_Flop j_k_ff_2 (.J(1'b1), .clk(out_3), .K(1'b1), .Qn(out_2), .reset(Clear_out));  // open: Q, preset
  J_K_Flip_Flop j_k_ff_3 (.J(1'b1), .clk(out_4), .K(1'b1), .Qn(out_3), .reset(Clear_out));  // open: Q, preset
  J_K_Flip_Flop j_k_ff_4 (.J(1'b1), .clk(out_5), .K(1'b1), .Qn(out_4), .reset(Clear_out));  // open: Q, preset
  J_K_Flip_Flop j_k_ff_5 (.J(1'b1), .clk(out_6), .K(1'b1), .Qn(out_5), .reset(Clear_out));  // open: Q, preset
  J_K_Flip_Flop j_k_ff_6 (.J(1'b1), .clk(pulse_out), .K(1'b1), .Qn(out_6), .reset(Clear_out));  // open: Q, preset

  // Notes on the sheet:
  //   Contador Decrescente (6 bits)
endmodule

module Contador_Crescente__6bits (
  output out_1,
  output out_2,
  output out_3,
  output out_4,
  output out_5,
  output out_6
);

  wire Clear_out, j_k_ff_1_qn, j_k_ff_2_qn, j_k_ff_3_qn, j_k_ff_4_qn, j_k_ff_5_qn, j_k_ff_6_qn, pulse_out;

  Button pulse (.out(pulse_out));
  Button Clear (.out(Clear_out));
  J_K_Flip_Flop j_k_ff_1 (
    .J(1'b1), .clk(j_k_ff_2_qn), .K(1'b1), .Qn(j_k_ff_1_qn), .reset(Clear_out));  // open: Q, preset
  J_K_Flip_Flop j_k_ff_2 (
    .J(1'b1), .clk(j_k_ff_3_qn), .K(1'b1), .Qn(j_k_ff_2_qn), .reset(Clear_out));  // open: Q, preset
  J_K_Flip_Flop j_k_ff_3 (
    .J(1'b1), .clk(j_k_ff_4_qn), .K(1'b1), .Qn(j_k_ff_3_qn), .reset(Clear_out));  // open: Q, preset
  J_K_Flip_Flop j_k_ff_4 (
    .J(1'b1), .clk(j_k_ff_5_qn), .K(1'b1), .Qn(j_k_ff_4_qn), .reset(Clear_out));  // open: Q, preset
  not not_1 (out_1, j_k_ff_1_qn);
  not not_2 (out_2, j_k_ff_2_qn);
  J_K_Flip_Flop j_k_ff_5 (
    .J(1'b1), .clk(j_k_ff_6_qn), .K(1'b1), .Qn(j_k_ff_5_qn), .reset(Clear_out));  // open: Q, preset
  not not_3 (out_4, j_k_ff_4_qn);
  not not_4 (out_5, j_k_ff_5_qn);
  not not_5 (out_3, j_k_ff_3_qn);
  not not_6 (out_6, j_k_ff_6_qn);
  J_K_Flip_Flop j_k_ff_6 (.J(1'b1), .clk(pulse_out), .K(1'b1), .Qn(j_k_ff_6_qn), .reset(Clear_out));  // open: Q, preset

  // Notes on the sheet:
  //   Contador Crescente (6bits)
endmodule

module Contador_Decadico_Crescente__5bits (
  output out_1,
  output out_2,
  output out_3,
  output out_4,
  output out_5
);

  wire and_1_out, Clear_out, j_k_ff_1_qn, j_k_ff_2_qn, j_k_ff_3_qn, j_k_ff_4_qn, not_1_out, not_2_out,
       not_3_out, or_1_out, pulse_out;

  Button pulse (.out(pulse_out));
  Button Clear (.out(Clear_out));
  not not_1 (not_1_out, out_1);
  or or_1 (or_1_out, Clear_out, and_1_out);
  not not_2 (not_2_out, out_5);
  not not_3 (not_3_out, out_3);
  and and_1 (and_1_out, not_1_out, out_2, not_3_out, out_4, not_2_out);
  J_K_Flip_Flop j_k_ff_1 (
    .J(1'b1), .clk(pulse_out), .K(1'b1), .Q(out_5), .Qn(j_k_ff_1_qn), .reset(or_1_out));  // open: preset
  J_K_Flip_Flop j_k_ff_2 (
    .J(1'b1), .clk(j_k_ff_1_qn), .K(1'b1), .Q(out_4), .Qn(j_k_ff_2_qn), .reset(or_1_out));  // open: preset
  J_K_Flip_Flop j_k_ff_3 (
    .J(1'b1), .clk(j_k_ff_2_qn), .K(1'b1), .Q(out_3), .Qn(j_k_ff_3_qn), .reset(or_1_out));  // open: preset
  J_K_Flip_Flop j_k_ff_4 (
    .J(1'b1), .clk(j_k_ff_3_qn), .K(1'b1), .Q(out_2), .Qn(j_k_ff_4_qn), .reset(or_1_out));  // open: preset
  J_K_Flip_Flop j_k_ff_5 (.J(1'b1), .clk(j_k_ff_4_qn), .K(1'b1), .Q(out_1), .reset(or_1_out));  // open: Qn, preset

  // Notes on the sheet:
  //   Contador Decadido Crescente (5bits)
endmodule

module Contador_Decadico_Decrescente__5bits (
  output out_1,
  output out_2,
  output out_3,
  output out_4,
  output out_5
);

  wire Clear_out, j_k_ff_5_qn, nor_1_out, or_1_out, pulse_out;

  Button pulse (.out(pulse_out));
  Button Clear (.out(Clear_out));
  nor nor_1 (nor_1_out, out_1, out_2, out_3, out_4, out_5);
  or or_1 (or_1_out, Clear_out, nor_1_out);
  J_K_Flip_Flop j_k_ff_1 (.J(1'b1), .clk(out_2), .K(1'b1), .Q(out_1), .reset(or_1_out));  // open: Qn, preset
  J_K_Flip_Flop j_k_ff_2 (.J(1'b1), .clk(out_3), .K(1'b1), .Qn(out_2), .reset(or_1_out));  // open: Q, preset
  J_K_Flip_Flop j_k_ff_3 (.J(1'b1), .clk(out_4), .K(1'b1), .Q(out_3), .reset(or_1_out));  // open: Qn, preset
  J_K_Flip_Flop j_k_ff_4 (.J(1'b1), .clk(out_5), .K(1'b1), .Qn(out_4), .reset(or_1_out));  // open: Q, preset
  J_K_Flip_Flop j_k_ff_5 (
    .J(1'b1), .clk(pulse_out), .K(1'b1), .Q(out_5), .Qn(j_k_ff_5_qn), .reset(or_1_out));  // open: preset

  // Notes on the sheet:
  //   Contador Decadico Decrescente (5bits)
endmodule

module Contador_Sincrono_Modulo_7 (
  input  Start,
  output out_2,
  output out_3,
  output out_4
);

  wire and_1_out, and_2_out, and_3_out, Clear_out, Clock_out, or_1_out;

  Clock Clock (.out(Clock_out));
  Button Clear (.out(Clear_out));
  and and_1 (and_1_out, out_2, out_3, out_4);
  or or_1 (or_1_out, Clear_out, and_1_out);
  T_Flip_Flop t_ff_1 (.clk(Clock_out), .T(Start), .Q(out_4), .reset(or_1_out));  // open: Qn, preset
  and and_2 (and_2_out, out_4, Start);
  T_Flip_Flop t_ff_2 (.clk(Clock_out), .T(and_2_out), .Q(out_3), .reset(or_1_out));  // open: Qn, preset
  and and_3 (and_3_out, out_3, and_2_out, Start);
  T_Flip_Flop t_ff_3 (.clk(Clock_out), .T(and_3_out), .Q(out_2), .reset(or_1_out));  // open: Qn, preset

  // Notes on the sheet:
  //   Contador Sincrono Modulo 7
endmodule

module Contador_de_Anel__6bits (
  output out_1,
  output out_2,
  output out_3,
  output out_4,
  output out_5,
  output out_6
);

  wire Clear_out, j_k_ff_1_qn, j_k_ff_2_qn, j_k_ff_3_qn, j_k_ff_4_qn, j_k_ff_5_qn, nor_1_out, not_1_out,
       Pulse_out;

  Button Pulse (.out(Pulse_out));
  Button Clear (.out(Clear_out));
  nor nor_1 (nor_1_out, out_1, out_2, out_3, out_4, out_5, out_6);
  not not_1 (not_1_out, out_6);
  J_K_Flip_Flop j_k_ff_1 (
    .J(out_6), .clk(Pulse_out), .K(not_1_out), .Q(out_1), .Qn(j_k_ff_1_qn), .preset(nor_1_out),
    .reset(Clear_out));
  J_K_Flip_Flop j_k_ff_2 (
    .J(out_1), .clk(Pulse_out), .K(j_k_ff_1_qn), .Q(out_2), .Qn(j_k_ff_2_qn), .reset(Clear_out));  // open: preset
  J_K_Flip_Flop j_k_ff_3 (
    .J(out_2), .clk(Pulse_out), .K(j_k_ff_2_qn), .Q(out_3), .Qn(j_k_ff_3_qn), .reset(Clear_out));  // open: preset
  J_K_Flip_Flop j_k_ff_4 (
    .J(out_3), .clk(Pulse_out), .K(j_k_ff_3_qn), .Q(out_4), .Qn(j_k_ff_4_qn), .reset(Clear_out));  // open: preset
  J_K_Flip_Flop j_k_ff_5 (
    .J(out_4), .clk(Pulse_out), .K(j_k_ff_4_qn), .Q(out_5), .Qn(j_k_ff_5_qn), .reset(Clear_out));  // open: preset
  J_K_Flip_Flop j_k_ff_6 (
    .J(out_5), .clk(Pulse_out), .K(j_k_ff_5_qn), .Q(out_6), .reset(Clear_out));  // open: Qn, preset

  // Notes on the sheet:
  //   Contador de Anel (6bits)
endmodule

module Contador_de_Anel_Torcido__6bits (
  output out_1,
  output out_2,
  output out_3,
  output out_4,
  output out_5,
  output out_6
);

  wire Clear_out, j_k_ff_1_qn, j_k_ff_2_qn, j_k_ff_3_qn, j_k_ff_4_qn, j_k_ff_5_qn, not_1_out, Pulse_out;

  Button Pulse (.out(Pulse_out));
  Button Clear (.out(Clear_out));
  not not_1 (not_1_out, out_6);
  J_K_Flip_Flop j_k_ff_1 (
    .J(not_1_out), .clk(Pulse_out), .K(out_6), .Q(out_1), .Qn(j_k_ff_1_qn), .reset(Clear_out));  // open: preset
  J_K_Flip_Flop j_k_ff_2 (
    .J(out_1), .clk(Pulse_out), .K(j_k_ff_1_qn), .Q(out_2), .Qn(j_k_ff_2_qn), .reset(Clear_out));  // open: preset
  J_K_Flip_Flop j_k_ff_3 (
    .J(out_2), .clk(Pulse_out), .K(j_k_ff_2_qn), .Q(out_3), .Qn(j_k_ff_3_qn), .reset(Clear_out));  // open: preset
  J_K_Flip_Flop j_k_ff_4 (
    .J(out_3), .clk(Pulse_out), .K(j_k_ff_3_qn), .Q(out_4), .Qn(j_k_ff_4_qn), .reset(Clear_out));  // open: preset
  J_K_Flip_Flop j_k_ff_5 (
    .J(out_4), .clk(Pulse_out), .K(j_k_ff_4_qn), .Q(out_5), .Qn(j_k_ff_5_qn), .reset(Clear_out));  // open: preset
  J_K_Flip_Flop j_k_ff_6 (
    .J(out_5), .clk(Pulse_out), .K(j_k_ff_5_qn), .Q(out_6), .reset(Clear_out));  // open: Qn, preset

  // Notes on the sheet:
  //   Contador de Anel Torcido (6bits)
endmodule
