// Logisim project logisim.circ as structural Verilog: 7 circuits, main circuit ex01
module ex01 (
  input  Data,
  output out_2,
  output out_3,
  output out_4,
  output \output ,
  output out_6,
  output out_7
);

  wire clear_out, Clock_out;

  Clock Clock (.out(Clock_out));
  Button clear (.out(clear_out));
  D_Flip_Flop d_ff_1 (.clk(Clock_out), .D(out_3), .Q(out_2), .reset(clear_out));  // open: Qn, preset
  D_Flip_Flop d_ff_2 (.clk(Clock_out), .D(out_4), .Q(out_3), .reset(clear_out));  // open: Qn, preset
  D_Flip_Flop d_ff_3 (.clk(Clock_out), .D(\output ), .Q(out_4), .reset(clear_out));  // open: Qn, preset
  D_Flip_Flop d_ff_4 (.clk(Clock_out), .D(out_6), .Q(\output ), .reset(clear_out));  // open: Qn, preset
  D_Flip_Flop d_ff_5 (.clk(Clock_out), .D(out_7), .Q(out_6), .reset(clear_out));  // open: Qn, preset
  D_Flip_Flop d_ff_6 (.clk(Clock_out), .D(Data), .Q(out_7), .preset(clear_out));  // open: Qn, reset

  // Notes on the sheet:
  //   registrador de deslocamento para a esquerda
endmodule

module ex02 (
  input  Data,
  output out_2,
  output out_3,
  output out_4,
  output \output ,
  output out_6,
  output out_7
);

  wire Clear_out, Clock_out;

  Clock Clock (.out(Clock_out));
  Button Clear (.out(Clear_out));
  D_Flip_Flop d_ff_1 (.clk(Clock_out), .D(out_3), .Q(out_2), .preset(Clear_out));  // open: Qn, reset
  D_Flip_Flop d_ff_2 (.clk(Clock_out), .D(out_4), .Q(out_3), .preset(Clear_out));  // open: Qn, reset
  D_Flip_Flop d_ff_3 (.clk(Clock_out), .D(\output ), .Q(out_4), .preset(Clear_out));  // open: Qn, reset
  D_Flip_Flop d_ff_4 (.clk(Clock_out), .D(out_6), .Q(\output ), .preset(Clear_out));  // open: Qn, reset
  D_Flip_Flop d_ff_5 (.clk(Clock_out), .D(out_7), .Q(out_6), .preset(Clear_out));  // open: Qn, reset
  D_Flip_Flop d_ff_6 (.clk(Clock_out), .D(Data), .Q(out_7), .preset(Clear_out));  // open: Qn, reset

  // Notes on the sheet:
  //   registrador de deslocamento para a esquerda
endmodule

module ex03 (
  output out_1,
  output out_2,
  output out_3,
  output out_4,
  output out_5,
  output out_6
);

  wire clear_out, Clock_out;

  Clock Clock (.out(Clock_out));
  Button clear (.out(clear_out));
  D_Flip_Flop d_ff_1 (.clk(Clock_out), .D(out_6), .Q(out_1), .preset(clear_out));  // open: Qn, reset
  D_Flip_Flop d_ff_2 (.clk(Clock_out), .D(out_1), .Q(out_2), .reset(clear_out));  // open: Qn, preset
  D_Flip_Flop d_ff_3 (.clk(Clock_out), .D(out_2), .Q(out_3), .reset(clear_out));  // open: Qn, preset
  D_Flip_Flop d_ff_4 (.clk(Clock_out), .D(out_3), .Q(out_4), .reset(clear_out));  // open: Qn, preset
  D_Flip_Flop d_ff_5 (.clk(Clock_out), .D(out_4), .Q(out_5), .reset(clear_out));  // open: Qn, preset
  D_Flip_Flop d_ff_6 (.clk(Clock_out), .D(out_5), .Q(out_6), .reset(clear_out));  // open: Qn, preset

  // Notes on the sheet:
  //   registrador de deslocamento circular ("ring") para a direita
  //   output
endmodule

module ex04 (
  output out_1,
  output out_2,
  output out_3,
  output \output ,
  output out_5,
  output out_6
);

  wire clear_out, Clock_out, not_1_out;

  Clock Clock (.out(Clock_out));
  Button clear (.out(clear_out));
  D_Flip_Flop d_ff_1 (.clk(Clock_out), .D(out_2), .Q(out_1), .reset(clear_out));  // open: Qn, preset
  D_Flip_Flop d_ff_2 (.clk(Clock_out), .D(out_3), .Q(out_2), .reset(clear_out));  // open: Qn, preset
  D_Flip_Flop d_ff_3 (.clk(Clock_out), .D(\output ), .Q(out_3), .reset(clear_out));  // open: Qn, preset
  D_Flip_Flop d_ff_4 (.clk(Clock_out), .D(out_5), .Q(\output ), .reset(clear_out));  // open: Qn, preset
  D_Flip_Flop d_ff_5 (.clk(Clock_out), .D(out_6), .Q(out_5), .reset(clear_out));  // open: Qn, preset
  not not_1 (not_1_out, out_1);
  D_Flip_Flop d_ff_6 (.clk(Clock_out), .D(not_1_out), .Q(out_6), .preset(clear_out));  // open: Qn, reset

  // Notes on the sheet:
  //   anel torcido ("twisted ring"), para a esquerda
endmodule

module ex05 (
  input  in_1,
  input  in_2,
  input  Input,
  input  in_4,
  input  in_5,
  input  in_6,
  input  ld,
  output out_8,
  output out_9,
  output out_10,
  output \output ,
  output out_12,
  output out_13
);

  wire and_1_out, and_2_out, and_3_out, and_4_out, and_5_out, and_6_out, clear_out, clock_out;

  Clock clock (.out(clock_out));
  Button clear (.out(clear_out));
  and and_1 (and_1_out, ld, in_1);
  D_Flip_Flop d_ff_1 (.clk(clock_out), .D(1'b0), .Q(out_8), .preset(and_1_out), .reset(clear_out));  // open: Qn
  and and_2 (and_2_out, ld, in_2);
  D_Flip_Flop d_ff_2 (.clk(clock_out), .D(out_8), .Q(out_9), .preset(and_2_out), .reset(clear_out));  // open: Qn
  and and_3 (and_3_out, ld, Input);
  D_Flip_Flop d_ff_3 (.clk(clock_out), .D(out_9), .Q(out_10), .preset(and_3_out), .reset(clear_out));  // open: Qn
  and and_4 (and_4_out, ld, in_4);
  D_Flip_Flop d_ff_4 (.clk(clock_out), .D(out_10), .Q(\output ), .preset(and_4_out), .reset(clear_out));  // open: Qn
  and and_5 (and_5_out, ld, in_5);
  D_Flip_Flop d_ff_5 (.clk(clock_out), .D(\output ), .Q(out_12), .preset(and_5_out), .reset(clear_out));  // open: Qn
  and and_6 (and_6_out, ld, in_6);
  D_Flip_Flop d_ff_6 (.clk(clock_out), .D(out_12), .Q(out_13), .preset(and_6_out), .reset(clear_out));  // open: Qn

  // Notes on the sheet:
  //   conversor paralelo-série
endmodule

module ex06 (
  output out_1,
  output out_2,
  output \output ,
  output out_4,
  output out_5
);

  wire clear_out, Clock_out, d_ff_1_q, d_ff_2_q, d_ff_3_q, d_ff_4_q, d_ff_5_q;

  Clock Clock (.out(Clock_out));
  Button clear (.out(clear_out));
  D_Flip_Flop d_ff_1 (.clk(Clock_out), .D(d_ff_5_q), .Q(d_ff_1_q), .Qn(out_5), .preset(clear_out));  // open: reset
  D_Flip_Flop d_ff_2 (.clk(Clock_out), .D(d_ff_1_q), .Q(d_ff_2_q), .Qn(out_4), .reset(clear_out));  // open: preset
  D_Flip_Flop d_ff_3 (.clk(Clock_out), .D(d_ff_2_q), .Q(d_ff_3_q), .Qn(\output ), .reset(clear_out));  // open: preset
  D_Flip_Flop d_ff_4 (.clk(Clock_out), .D(d_ff_3_q), .Q(d_ff_4_q), .Qn(out_2), .reset(clear_out));  // open: preset
  D_Flip_Flop d_ff_5 (.clk(Clock_out), .D(d_ff_4_q), .Q(d_ff_5_q), .Qn(out_1), .reset(clear_out));  // open: preset

  // Notes on the sheet:
  //   registrador de deslocamento circular ("ring") para a esquerda
endmodule

module ex07 (
  output out_1,
  output out_2,
  output \output ,
  output out_4,
  output out_5
);

  wire clear_out, Clock_out, not_1_out;

  Clock Clock (.out(Clock_out));
  Button clear (.out(clear_out));
  D_Flip_Flop d_ff_1 (.clk(Clock_out), .D(out_2), .Q(out_1), .preset(clear_out));  // open: Qn, reset
  D_Flip_Flop d_ff_2 (.clk(Clock_out), .D(\output ), .Q(out_2), .preset(clear_out));  // open: Qn, reset
  D_Flip_Flop d_ff_3 (.clk(Clock_out), .D(out_4), .Q(\output ), .preset(clear_out));  // open: Qn, reset
  D_Flip_Flop d_ff_4 (.clk(Clock_out), .D(out_5), .Q(out_4), .preset(clear_out));  // open: Qn, reset
  not not_1 (not_1_out, out_1);
  D_Flip_Flop d_ff_5 (.clk(Clock_out), .D(not_1_out), .Q(out_5), .preset(clear_out));  // open: Qn, reset

  // Notes on the sheet:
  //   anel torcido ("twisted ring"), para a direita
endmodule
