// Logisim project Questao 1, 2 e 3.circ as structural Verilog: 1 circuit, main circuit main
module main (
  input  a_b,
  input  a,
  input  b,
  input  a_b_2,
  output out_5,
  output out_6,
  output out_7
);

  wire Clock_2_out, Clock_3_out, Clock_out, not_1_out;

  Clock Clock (.out(Clock_out));
  Clock Clock_2 (.out(Clock_2_out));
  Clock Clock_3 (.out(Clock_3_out));
  J_K_Flip_Flop j_k_ff_1 (.J(a_b), .clk(Clock_out), .K(not_1_out), .Q(out_5));  // open: Qn, preset, reset
  not not_1 (not_1_out, a_b);
  J_K_Flip_Flop j_k_ff_2 (.J(a), .clk(Clock_2_out), .K(b), .Q(out_6));  // open: Qn, preset, reset
  J_K_Flip_Flop j_k_ff_3 (.J(a_b_2), .clk(Clock_3_out), .K(a_b_2), .Q(out_7));  // open: Qn, preset, reset

  // Notes on the sheet:
  //   JK em modo D
  //   JK em modo SR
  //   JK em modo T (toggle)
endmodule
