// Logisim project Questao 4 e 5.circ as structural Verilog: 1 circuit, main circuit main
module main (
  output Q3,
  output Q2,
  output Q1,
  output Q3_2,
  output Q2_2,
  output Q1_2
);

  wire Clear_2_out, Clear_out, Clock_2_out, Clock_out, t1_2_qn, t2_2_qn;

  Clock Clock (.out(Clock_out));
  Button Clear (.out(Clear_out));
  Clock Clock_2 (.out(Clock_2_out));
  Button Clear_2 (.out(Clear_2_out));
  T_Flip_Flop t1 (.clk(Clock_out), .T(1'b1), .Q(Q1), .reset(Clear_out));  // open: Qn, preset
  T_Flip_Flop t1_2 (.clk(Clock_2_out), .T(1'b1), .Q(Q1_2), .Qn(t1_2_qn), .reset(Clear_2_out));  // open: preset
  T_Flip_Flop t2 (.clk(Q1), .T(1'b1), .Q(Q2), .reset(Clear_out));  // open: Qn, preset
  T_Flip_Flop t2_2 (.clk(t1_2_qn), .T(1'b1), .Q(Q2_2), .Qn(t2_2_qn), .reset(Clear_2_out));  // open: preset
  T_Flip_Flop t3 (.clk(Q2), .T(1'b1), .Q(Q3), .reset(Clear_out));  // open: Qn, preset
  T_Flip_Flop t3_2 (.clk(t2_2_qn), .T(1'b1), .Q(Q3_2), .reset(Clear_2_out));  // open: Qn, preset

  // Notes on the sheet:
  //   Questao 04
  //   Questao 05
endmodule
