// Logisim project Questao01.circ as structural Verilog: 4 circuits, main circuit SoP Simplificada
module SoP_Canonica (
  input  a,
  input  b,
  input  c,
  input  d,
  output Saida
);

  wire and_1_out, and_2_out, and_3_out, and_4_out, and_5_out, and_6_out, and_7_out, and_8_out, not_1_out,
       not_2_out, not_3_out, not_4_out, not_5_out, not_6_out, not_7_out, not_8_out, not_9_out, not_10_out,
       not_11_out, not_12_out, not_13_out, not_14_out, not_15_out, not_16_out, not_17_out, not_18_out,
       not_19_out;

  not not_1 (not_1_out, a);
  not not_2 (not_2_out, b);
  not not_3 (not_3_out, c);
  not not_4 (not_4_out, d);
  not not_5 (not_5_out, a);
  not not_6 (not_6_out, b);
  not not_7 (not_7_out, c);
  not not_8 (not_8_out, a);
  not not_9 (not_9_out, c);
  not not_10 (not_10_out, a);
  not not_11 (not_11_out, d);
  not not_12 (not_12_out, b);
  not not_13 (not_13_out, c);
  not not_14 (not_14_out, d);
  not not_15 (not_15_out, b);
  not not_16 (not_16_out, c);
  not not_17 (not_17_out, c);
  not not_18 (not_18_out, d);
  not not_19 (not_19_out, d);
  and and_1 (and_1_out, not_1_out, not_2_out, not_3_out, not_4_out);
  and and_2 (and_2_out, not_5_out, not_6_out, not_7_out, d);
  and and_3 (and_3_out, not_8_out, b, not_9_out, d);
  and and_4 (and_4_out, not_10_out, b, c, not_11_out);
  and and_5 (and_5_out, a, not_12_out, not_13_out, not_14_out);
  and and_6 (and_6_out, a, not_15_out, not_16_out, d);
  and and_7 (and_7_out, a, b, not_17_out, not_18_out);
  and and_8 (and_8_out, a, b, c, not_19_out);
  or or_1 (Saida, and_1_out, and_2_out, and_3_out, and_4_out, and_5_out, and_6_out, and_7_out, and_8_out);

  // Notes on the sheet:
  //   SoP Canonica
  //   (a'.b'.c'.d') +  (a'.b'.c'.d ) +  (a'.b .c'.d ) +  (a'.b .c .d') +  (a .b'.c'.d') +  (a .b'.c'.d ) +  (a .b .c'.d') +  (a .b .c .d')
endmodule

module SoP_Simplificada (
  input  a,
  input  b,
  input  c,
  input  d,
  output Saida
);

  wire and_1_out, and_2_out, and_3_out, and_4_out, not_1_out, not_2_out, not_3_out, not_4_out, not_5_out,
       not_6_out, not_7_out;

  not not_1 (not_1_out, b);
  not not_2 (not_2_out, c);
  not not_3 (not_3_out, a);
  not not_4 (not_4_out, c);
  not not_5 (not_5_out, c);
  not not_6 (not_6_out, d);
  not not_7 (not_7_out, d);
  and and_1 (and_1_out, not_1_out, not_2_out);
  and and_2 (and_2_out, not_3_out, not_4_out, d);
  and and_3 (and_3_out, a, not_5_out, not_6_out);
  and and_4 (and_4_out, b, c, not_7_out);
  or or_1 (Saida, and_1_out, and_2_out, and_3_out, and_4_out);

  // Notes on the sheet:
  //   SoP
  //   (b'.c') + (a'.c'.d) + (a.c'.d') + (b.c.d')
endmodule

module PoS_Canonica (
  input  a,
  input  b,
  input  c,
  input  d,
  output Saida
);

  wire not_1_out, not_2_out, not_3_out, not_4_out, not_5_out, not_6_out, not_7_out, not_8_out, not_9_out,
       not_10_out, not_11_out, not_12_out, not_13_out, not_14_out, not_15_out, not_16_out, not_17_out,
       not_18_out, not_19_out, or_1_out, or_2_out, or_3_out, or_4_out, or_5_out, or_6_out, or_7_out, or_8_out;

  not not_1 (not_1_out, c);
  not not_2 (not_2_out, c);
  not not_3 (not_3_out, d);
  not not_4 (not_4_out, b);
  not not_5 (not_5_out, b);
  not not_6 (not_6_out, c);
  not not_7 (not_7_out, d);
  not not_8 (not_8_out, a);
  not not_9 (not_9_out, c);
  not not_10 (not_10_out, a);
  not not_11 (not_11_out, c);
  not not_12 (not_12_out, d);
  not not_13 (not_13_out, a);
  not not_14 (not_14_out, b);
  not not_15 (not_15_out, d);
  not not_16 (not_16_out, a);
  not not_17 (not_17_out, b);
  not not_18 (not_18_out, c);
  not not_19 (not_19_out, d);
  or or_1 (or_1_out, a, b, not_1_out, d);
  or or_2 (or_2_out, a, b, not_2_out, not_3_out);
  or or_3 (or_3_out, a, not_4_out, c, d);
  or or_4 (or_4_out, a, not_5_out, not_6_out, not_7_out);
  or or_5 (or_5_out, not_8_out, b, not_9_out, d);
  or or_6 (or_6_out, not_10_out, b, not_11_out, not_12_out);
  or or_7 (or_7_out, not_13_out, not_14_out, c, not_15_out);
  or or_8 (or_8_out, not_16_out, not_17_out, not_18_out, not_19_out);
  and and_1 (Saida, or_1_out, or_2_out, or_3_out, or_4_out, or_5_out, or_6_out, or_7_out, or_8_out);

  // Notes on the sheet:
  //   PoS Canonica
  //   (A +B +C'+D ) . (A +B +C'+D') . (A +B'+C +D ) . (A +B'+C'+D') . (A'+B +C'+D ) . (A'+B +C'+D') . (A'+B'+C +D') . (A'+B'+C'+D')
endmodule

module PoS_Simplificada (
  input  a,
  input  b,
  input  c,
  input  d,
  output Saida
);

  wire not_1_out, not_2_out, not_3_out, not_4_out, not_5_out, not_6_out, not_7_out, or_1_out, or_2_out,
       or_3_out, or_4_out;

  not not_1 (not_1_out, c);
  not not_2 (not_2_out, d);
  not not_3 (not_3_out, c);
  not not_4 (not_4_out, a);
  not not_5 (not_5_out, b);
  not not_6 (not_6_out, d);
  not not_7 (not_7_out, b);
  or or_1 (or_1_out, not_1_out, not_2_out);
  or or_2 (or_2_out, b, not_3_out);
  or or_3 (or_3_out, not_4_out, not_5_out, not_6_out);
  or or_4 (or_4_out, a, not_7_out, c, d);
  and and_1 (Saida, or_1_out, or_2_out, or_3_out, or_4_out);

  // Notes on the sheet:
  //   PoS
  //   (C'+D') . (B +C') . (A'+B'+D') . (A +B'+C +D )
endmodule
