// Logisim project Questao04.circ as structural Verilog: 3 circuits, main circuit Letra_A
module Letra_A (
  input  a,
  input  b,
  input  c,
  output out_4
);

  wire nor_1_out, nor_2_out, nor_3_out;

  nor nor_1 (nor_1_out, a, a);
  nor nor_2 (nor_2_out, nor_3_out, nor_3_out);
  nor nor_3 (nor_3_out, nor_1_out, b);
  nor nor_4 (out_4, nor_2_out, c);

  // Notes on the sheet:
  //   m | 0 | 1 | 2 | 3 | 4 | 5 | 6 | 7 
  //     | 0 | 0 | 0 | 0 | 1 | 0 | 0 | 0 
  //   a.) nor ( nor ( nor ( nor (a,a),b ), nor ( nor(a,a),b) ), c )
endmodule

module Letra_B (
  input  a,
  input  b,
  input  c,
  output out_4
);

  wire nand_1_out, nand_2_out, nand_3_out, nand_4_out;

  nand nand_1 (nand_1_out, a, a);
  nand nand_2 (nand_2_out, b, b);
  nand nand_3 (nand_3_out, nand_1_out, b);
  nand nand_4 (nand_4_out, a, nand_2_out);
  nand nand_5 (out_4, nand_3_out, nand_4_out);

  // Notes on the sheet:
  //   b.) nand ( nand ( nand(a,a), b ),nand ( a,nand(b,b) ) ) 
  //   m | 0 | 1 | 2 | 3 | 4 | 5 | 6 | 7
  //     | 0 | 0 | 1 | 1 | 1 | 1 | 0 | 0 
endmodule

module Letra_C (
  input  a,
  input  b,
  input  c,
  output out_4
);

  wire multiplexer_1_out, multiplexer_2_out, not_1_out;

  Multiplexer #(.enable("false")) multiplexer_1 (.in0(b), .in1(c), .out(multiplexer_1_out), .sel(a));
  not not_1 (not_1_out, a);
  Multiplexer #(.enable("false")) multiplexer_2 (.in0(not_1_out), .in1(b), .out(multiplexer_2_out), .sel(c));
  Multiplexer #(.enable("false")) multiplexer_3 (
    .in0(multiplexer_1_out), .in1(multiplexer_2_out), .out(out_4), .sel(c));

  // Notes on the sheet:
  //   c.) mux ( mux(b,c,a), mux(not(a),b,c), not(c) ) 
  //   m | 0 | 1 | 2 | 3 | 4 | 5 | 6 | 7
  //     | 0 | 0 | 1 | 1 | 0 | 0 | 0 | 1 
endmodule
